// Logisim project banco-reg-32bit.circ as structural Verilog: 4 circuits, main circuit registrador-32bit
module banco_32bit (
  input  [31:0] Data,
  input  Reset,
  input  [4:0] Reg1,
  input  [4:0] Reg2,
  input  CLK,
  input  [4:0] WReg,
  output [31:0] ViewReg1,
  output Zero1,
  output [31:0] ViewReg2,
  output Zero2
);

  wire demultiplexer_1_out0, demultiplexer_1_out1, demultiplexer_1_out2, demultiplexer_1_out3,
       demultiplexer_1_out4, demultiplexer_1_out5, demultiplexer_1_out6, demultiplexer_1_out7,
       demultiplexer_1_out8, demultiplexer_1_out9, demultiplexer_1_out10, demultiplexer_1_out11,
       demultiplexer_1_out12, demultiplexer_1_out13, demultiplexer_1_out14, demultiplexer_1_out15,
       demultiplexer_1_out16, demultiplexer_1_out17, demultiplexer_1_out18, demultiplexer_1_out19,
       demultiplexer_1_out20, demultiplexer_1_out21, demultiplexer_1_out22, demultiplexer_1_out23,
       demultiplexer_1_out24, demultiplexer_1_out25, demultiplexer_1_out26, demultiplexer_1_out27,
       demultiplexer_1_out28, demultiplexer_1_out29, demultiplexer_1_out30, demultiplexer_1_out31;
  wire [31:0] registrador_32bit_1_out_4, registrador_32bit_2_out_4, registrador_32bit_3_out_4,
       registrador_32bit_4_out_4, registrador_32bit_5_out_4, registrador_32bit_6_out_4,
       registrador_32bit_7_out_4, registrador_32bit_8_out_4, registrador_32bit_9_out_4,
       registrador_32bit_10_out_4, registrador_32bit_11_out_4, registrador_32bit_12_out_4,
       registrador_32bit_13_out_4, registrador_32bit_14_out_4, registrador_32bit_15_out_4,
       registrador_32bit_16_out_4, registrador_32bit_17_out_4, registrador_32bit_18_out_4,
       registrador_32bit_19_out_4, registrador_32bit_20_out_4, registrador_32bit_21_out_4,
       registrador_32bit_22_out_4, registrador_32bit_23_out_4, registrador_32bit_24_out_4,
       registrador_32bit_25_out_4, registrador_32bit_26_out_4, registrador_32bit_27_out_4,
       registrador_32bit_28_out_4, registrador_32bit_29_out_4, registrador_32bit_30_out_4,
       registrador_32bit_31_out_4, registrador_32bit_32_out_4;

  Demultiplexer #(.select(5), .enable("false")) demultiplexer_1 (
    .out0(demultiplexer_1_out0), .out1(demultiplexer_1_out1), .out2(demultiplexer_1_out2),
    .out3(demultiplexer_1_out3), .out4(demultiplexer_1_out4), .out5(demultiplexer_1_out5),
    .out6(demultiplexer_1_out6), .out7(demultiplexer_1_out7), .out8(demultiplexer_1_out8),
    .out9(demultiplexer_1_out9), .out10(demultiplexer_1_out10), .out11(demultiplexer_1_out11),
    .out12(demultiplexer_1_out12), .out13(demultiplexer_1_out13), .out14(demultiplexer_1_out14),
    .out15(demultiplexer_1_out15), .out16(demultiplexer_1_out16), .out17(demultiplexer_1_out17),
    .out18(demultiplexer_1_out18), .out19(demultiplexer_1_out19), .out20(demultiplexer_1_out20),
    .out21(demultiplexer_1_out21), .out22(demultiplexer_1_out22), .out23(demultiplexer_1_out23),
    .out24(demultiplexer_1_out24), .out25(demultiplexer_1_out25), .out26(demultiplexer_1_out26),
    .out27(demultiplexer_1_out27), .out28(demultiplexer_1_out28), .out29(demultiplexer_1_out29),
    .out30(demultiplexer_1_out30), .out31(demultiplexer_1_out31), .in(CLK), .sel(WReg));
  registrador_32bit registrador_32bit_1 (
    .DataIn(Data), .Save(demultiplexer_1_out0), .Reset(Reset), .out_4(registrador_32bit_1_out_4));
  registrador_32bit registrador_32bit_2 (
    .DataIn(Data), .Save(demultiplexer_1_out1), .Reset(Reset), .out_4(registrador_32bit_2_out_4));
  registrador_32bit registrador_32bit_3 (
    .DataIn(Data), .Save(demultiplexer_1_out2), .Reset(Reset), .out_4(registrador_32bit_3_out_4));
  registrador_32bit registrador_32bit_4 (
    .DataIn(Data), .Save(demultiplexer_1_out3), .Reset(Reset), .out_4(registrador_32bit_4_out_4));
  registrador_32bit registrador_32bit_5 (
    .DataIn(Data), .Save(demultiplexer_1_out4), .Reset(Reset), .out_4(registrador_32bit_5_out_4));
  registrador_32bit registrador_32bit_6 (
    .DataIn(Data), .Save(demultiplexer_1_out5), .Reset(Reset), .out_4(registrador_32bit_6_out_4));
  registrador_32bit registrador_32bit_7 (
    .DataIn(Data), .Save(demultiplexer_1_out6), .Reset(Reset), .out_4(registrador_32bit_7_out_4));
  registrador_32bit registrador_32bit_8 (
    .DataIn(Data), .Save(demultiplexer_1_out7), .Reset(Reset), .out_4(registrador_32bit_8_out_4));
  registrador_32bit registrador_32bit_9 (
    .DataIn(Data), .Save(demultiplexer_1_out8), .Reset(Reset), .out_4(registrador_32bit_9_out_4));
  registrador_32bit registrador_32bit_10 (
    .DataIn(Data), .Save(demultiplexer_1_out9), .Reset(Reset), .out_4(registrador_32bit_10_out_4));
  registrador_32bit registrador_32bit_11 (
    .DataIn(Data), .Save(demultiplexer_1_out10), .Reset(Reset), .out_4(registrador_32bit_11_out_4));
  registrador_32bit registrador_32bit_12 (
    .DataIn(Data), .Save(demultiplexer_1_out11), .Reset(Reset), .out_4(registrador_32bit_12_out_4));
  registrador_32bit registrador_32bit_13 (
    .DataIn(Data), .Save(demultiplexer_1_out12), .Reset(Reset), .out_4(registrador_32bit_13_out_4));
  registrador_32bit registrador_32bit_14 (
    .DataIn(Data), .Save(demultiplexer_1_out13), .Reset(Reset), .out_4(registrador_32bit_14_out_4));
  registrador_32bit registrador_32bit_15 (
    .DataIn(Data), .Save(demultiplexer_1_out14), .Reset(Reset), .out_4(registrador_32bit_15_out_4));
  registrador_32bit registrador_32bit_16 (
    .DataIn(Data), .Save(demultiplexer_1_out15), .Reset(Reset), .out_4(registrador_32bit_16_out_4));
  registrador_32bit registrador_32bit_17 (
    .DataIn(Data), .Save(demultiplexer_1_out16), .Reset(Reset), .out_4(registrador_32bit_17_out_4));
  registrador_32bit registrador_32bit_18 (
    .DataIn(Data), .Save(demultiplexer_1_out17), .Reset(Reset), .out_4(registrador_32bit_18_out_4));
  registrador_32bit registrador_32bit_19 (
    .DataIn(Data), .Save(demultiplexer_1_out18), .Reset(Reset), .out_4(registrador_32bit_19_out_4));
  registrador_32bit registrador_32bit_20 (
    .DataIn(Data), .Save(demultiplexer_1_out19), .Reset(Reset), .out_4(registrador_32bit_20_out_4));
  registrador_32bit registrador_32bit_21 (
    .DataIn(Data), .Save(demultiplexer_1_out20), .Reset(Reset), .out_4(registrador_32bit_21_out_4));
  registrador_32bit registrador_32bit_22 (
    .DataIn(Data), .Save(demultiplexer_1_out21), .Reset(Reset), .out_4(registrador_32bit_22_out_4));
  registrador_32bit registrador_32bit_23 (
    .DataIn(Data), .Save(demultiplexer_1_out22), .Reset(Reset), .out_4(registrador_32bit_23_out_4));
  registrador_32bit registrador_32bit_24 (
    .DataIn(Data), .Save(demultiplexer_1_out23), .Reset(Reset), .out_4(registrador_32bit_24_out_4));
  registrador_32bit registrador_32bit_25 (
    .DataIn(Data), .Save(demultiplexer_1_out24), .Reset(Reset), .out_4(registrador_32bit_25_out_4));
  registrador_32bit registrador_32bit_26 (
    .DataIn(Data), .Save(demultiplexer_1_out25), .Reset(Reset), .out_4(registrador_32bit_26_out_4));
  registrador_32bit registrador_32bit_27 (
    .DataIn(Data), .Save(demultiplexer_1_out26), .Reset(Reset), .out_4(registrador_32bit_27_out_4));
  registrador_32bit registrador_32bit_28 (
    .DataIn(Data), .Save(demultiplexer_1_out27), .Reset(Reset), .out_4(registrador_32bit_28_out_4));
  registrador_32bit registrador_32bit_29 (
    .DataIn(Data), .Save(demultiplexer_1_out28), .Reset(Reset), .out_4(registrador_32bit_29_out_4));
  registrador_32bit registrador_32bit_30 (
    .DataIn(Data), .Save(demultiplexer_1_out29), .Reset(Reset), .out_4(registrador_32bit_30_out_4));
  registrador_32bit registrador_32bit_31 (
    .DataIn(Data), .Save(demultiplexer_1_out30), .Reset(Reset), .out_4(registrador_32bit_31_out_4));
  registrador_32bit registrador_32bit_32 (
    .DataIn(Data), .Save(demultiplexer_1_out31), .Reset(Reset), .out_4(registrador_32bit_32_out_4));
  Multiplexer #(.select(5), .width(32), .enable("false")) multiplexer_1 (
    .in0(registrador_32bit_1_out_4), .in1(registrador_32bit_2_out_4), .in2(registrador_32bit_3_out_4),
    .in3(registrador_32bit_4_out_4), .in4(registrador_32bit_5_out_4), .in5(registrador_32bit_6_out_4),
    .in6(registrador_32bit_7_out_4), .in7(registrador_32bit_8_out_4), .in8(registrador_32bit_9_out_4),
    .in9(registrador_32bit_10_out_4), .in10(registrador_32bit_11_out_4), .in11(registrador_32bit_12_out_4),
    .in12(registrador_32bit_13_out_4), .in13(registrador_32bit_14_out_4), .in14(registrador_32bit_15_out_4),
    .in15(registrador_32bit_16_out_4), .in16(registrador_32bit_17_out_4), .in17(registrador_32bit_18_out_4),
    .in18(registrador_32bit_19_out_4), .in19(registrador_32bit_20_out_4), .in20(registrador_32bit_21_out_4),
    .in21(registrador_32bit_22_out_4), .in22(registrador_32bit_23_out_4), .in23(registrador_32bit_24_out_4),
    .in24(registrador_32bit_25_out_4), .in25(registrador_32bit_26_out_4), .in26(registrador_32bit_27_out_4),
    .in27(registrador_32bit_28_out_4), .in28(registrador_32bit_29_out_4), .in29(registrador_32bit_30_out_4),
    .in30(registrador_32bit_31_out_4), .in31(registrador_32bit_32_out_4), .out(ViewReg1), .sel(Reg1));
  Multiplexer #(.select(5), .width(32), .enable("false")) multiplexer_2 (
    .in0(registrador_32bit_1_out_4), .in1(registrador_32bit_2_out_4), .in2(registrador_32bit_3_out_4),
    .in3(registrador_32bit_4_out_4), .in4(registrador_32bit_5_out_4), .in5(registrador_32bit_6_out_4),
    .in6(registrador_32bit_7_out_4), .in7(registrador_32bit_8_out_4), .in8(registrador_32bit_9_out_4),
    .in9(registrador_32bit_10_out_4), .in10(registrador_32bit_11_out_4), .in11(registrador_32bit_12_out_4),
    .in12(registrador_32bit_13_out_4), .in13(registrador_32bit_14_out_4), .in14(registrador_32bit_15_out_4),
    .in15(registrador_32bit_16_out_4), .in16(registrador_32bit_17_out_4), .in17(registrador_32bit_18_out_4),
    .in18(registrador_32bit_19_out_4), .in19(registrador_32bit_20_out_4), .in20(registrador_32bit_21_out_4),
    .in21(registrador_32bit_22_out_4), .in22(registrador_32bit_23_out_4), .in23(registrador_32bit_24_out_4),
    .in24(registrador_32bit_25_out_4), .in25(registrador_32bit_26_out_4), .in26(registrador_32bit_27_out_4),
    .in27(registrador_32bit_28_out_4), .in28(registrador_32bit_29_out_4), .in29(registrador_32bit_30_out_4),
    .in30(registrador_32bit_31_out_4), .in31(registrador_32bit_32_out_4), .out(ViewReg2), .sel(Reg2));
  and and_1 (Zero1, ~ViewReg1[16], ~ViewReg1[31], ~ViewReg1[30], ~ViewReg1[29], ~ViewReg1[28], ~ViewReg1[27], ~ViewReg1[26], ~ViewReg1[25], ~ViewReg1[24], ~ViewReg1[23], ~ViewReg1[22], ~ViewReg1[21], ~ViewReg1[20], ~ViewReg1[19], ~ViewReg1[18], ~ViewReg1[17], ~ViewReg1[15], ~ViewReg1[14], ~ViewReg1[13], ~ViewReg1[12], ~ViewReg1[11], ~ViewReg1[10], ~ViewReg1[9], ~ViewReg1[8], ~ViewReg1[7], ~ViewReg1[6], ~ViewReg1[5], ~ViewReg1[4], ~ViewReg1[3], ~ViewReg1[2], ~ViewReg1[1], ~ViewReg1[0]);  // AND_Gate
  and and_2 (Zero2, ~ViewReg2[16], ~ViewReg2[31], ~ViewReg2[30], ~ViewReg2[29], ~ViewReg2[28], ~ViewReg2[27], ~ViewReg2[26], ~ViewReg2[25], ~ViewReg2[24], ~ViewReg2[23], ~ViewReg2[22], ~ViewReg2[21], ~ViewReg2[20], ~ViewReg2[19], ~ViewReg2[18], ~ViewReg2[17], ~ViewReg2[15], ~ViewReg2[14], ~ViewReg2[13], ~ViewReg2[12], ~ViewReg2[11], ~ViewReg2[10], ~ViewReg2[9], ~ViewReg2[8], ~ViewReg2[7], ~ViewReg2[6], ~ViewReg2[5], ~ViewReg2[4], ~ViewReg2[3], ~ViewReg2[2], ~ViewReg2[1], ~ViewReg2[0]);  // AND_Gate
endmodule

module registrador_32bit (
  input  [31:0] DataIn,
  input  Save,
  input  Reset,
  output [31:0] out_4
);

  D_Flip_Flop d_ff_1 (.clk(Save), .D(DataIn[31]), .Q(out_4[31]), .reset(Reset));  // open: Qn, preset, en
  D_Flip_Flop d_ff_2 (.clk(Save), .D(DataIn[30]), .Q(out_4[30]), .reset(Reset));  // open: Qn, preset, en
  D_Flip_Flop d_ff_3 (.clk(Save), .D(DataIn[29]), .Q(out_4[29]), .reset(Reset));  // open: Qn, preset, en
  D_Flip_Flop d_ff_4 (.clk(Save), .D(DataIn[28]), .Q(out_4[28]), .reset(Reset));  // open: Qn, preset, en
  D_Flip_Flop d_ff_5 (.clk(Save), .D(DataIn[27]), .Q(out_4[27]), .reset(Reset));  // open: Qn, preset, en
  D_Flip_Flop d_ff_6 (.clk(Save), .D(DataIn[26]), .Q(out_4[26]), .reset(Reset));  // open: Qn, preset, en
  D_Flip_Flop d_ff_7 (.clk(Save), .D(DataIn[25]), .Q(out_4[25]), .reset(Reset));  // open: Qn, preset, en
  D_Flip_Flop d_ff_8 (.clk(Save), .D(DataIn[24]), .Q(out_4[24]), .reset(Reset));  // open: Qn, preset, en
  D_Flip_Flop d_ff_9 (.clk(Save), .D(DataIn[23]), .Q(out_4[23]), .reset(Reset));  // open: Qn, preset, en
  D_Flip_Flop d_ff_10 (.clk(Save), .D(DataIn[22]), .Q(out_4[22]), .reset(Reset));  // open: Qn, preset, en
  D_Flip_Flop d_ff_11 (.clk(Save), .D(DataIn[21]), .Q(out_4[21]), .reset(Reset));  // open: Qn, preset, en
  D_Flip_Flop d_ff_12 (.clk(Save), .D(DataIn[20]), .Q(out_4[20]), .reset(Reset));  // open: Qn, preset, en
  D_Flip_Flop d_ff_13 (.clk(Save), .D(DataIn[19]), .Q(out_4[19]), .reset(Reset));  // open: Qn, preset, en
  D_Flip_Flop d_ff_14 (.clk(Save), .D(DataIn[18]), .Q(out_4[18]), .reset(Reset));  // open: Qn, preset, en
  D_Flip_Flop d_ff_15 (.clk(Save), .D(DataIn[17]), .Q(out_4[17]), .reset(Reset));  // open: Qn, preset, en
  D_Flip_Flop d_ff_16 (.clk(Save), .D(DataIn[16]), .Q(out_4[16]), .reset(Reset));  // open: Qn, preset, en
  D_Flip_Flop d_ff_17 (.clk(Save), .D(DataIn[15]), .Q(out_4[15]), .reset(Reset));  // open: Qn, preset, en
  D_Flip_Flop d_ff_18 (.clk(Save), .D(DataIn[14]), .Q(out_4[14]), .reset(Reset));  // open: Qn, preset, en
  D_Flip_Flop d_ff_19 (.clk(Save), .D(DataIn[13]), .Q(out_4[13]), .reset(Reset));  // open: Qn, preset, en
  D_Flip_Flop d_ff_20 (.clk(Save), .D(DataIn[12]), .Q(out_4[12]), .reset(Reset));  // open: Qn, preset, en
  D_Flip_Flop d_ff_21 (.clk(Save), .D(DataIn[11]), .Q(out_4[11]), .reset(Reset));  // open: Qn, preset, en
  D_Flip_Flop d_ff_22 (.clk(Save), .D(DataIn[10]), .Q(out_4[10]), .reset(Reset));  // open: Qn, preset, en
  D_Flip_Flop d_ff_23 (.clk(Save), .D(DataIn[9]), .Q(out_4[9]), .reset(Reset));  // open: Qn, preset, en
  D_Flip_Flop d_ff_24 (.clk(Save), .D(DataIn[8]), .Q(out_4[8]), .reset(Reset));  // open: Qn, preset, en
  D_Flip_Flop d_ff_25 (.clk(Save), .D(DataIn[7]), .Q(out_4[7]), .reset(Reset));  // open: Qn, preset, en
  D_Flip_Flop d_ff_26 (.clk(Save), .D(DataIn[6]), .Q(out_4[6]), .reset(Reset));  // open: Qn, preset, en
  D_Flip_Flop d_ff_27 (.clk(Save), .D(DataIn[5]), .Q(out_4[5]), .reset(Reset));  // open: Qn, preset, en
  D_Flip_Flop d_ff_28 (.clk(Save), .D(DataIn[4]), .Q(out_4[4]), .reset(Reset));  // open: Qn, preset, en
  D_Flip_Flop d_ff_29 (.clk(Save), .D(DataIn[3]), .Q(out_4[3]), .reset(Reset));  // open: Qn, preset, en
  D_Flip_Flop d_ff_30 (.clk(Save), .D(DataIn[2]), .Q(out_4[2]), .reset(Reset));  // open: Qn, preset, en
  D_Flip_Flop d_ff_31 (.clk(Save), .D(DataIn[1]), .Q(out_4[1]), .reset(Reset));  // open: Qn, preset, en
  D_Flip_Flop d_ff_32 (.clk(Save), .D(DataIn[0]), .Q(out_4[0]), .reset(Reset));  // open: Qn, preset, en
endmodule

module teste (
  input  [31:0] DataIn,
  input  CLK,
  input  [4:0] WReg,
  input  Reset,
  input  [4:0] Reg1,
  input  [4:0] Reg2,
  output [31:0] ViewReg1,
  output Zero1,
  output [31:0] ViewReg2,
  output Zero2
);

  banco_32bit banco_32bit_1 (
    .CLK(CLK), .Data(DataIn), .Reset(Reset), .WReg(WReg), .Reg1(Reg1), .Reg2(Reg2), .ViewReg1(ViewReg1),
    .Zero1(Zero1), .ViewReg2(ViewReg2), .Zero2(Zero2));
endmodule

module dois_bancos (
  input  [31:0] DATAIN,
  input  CLK,
  input  CONTEXTO,
  input  RESET,
  input  [4:0] WReg,
  input  [4:0] Reg1,
  input  [4:0] Reg2,
  output [31:0] View1,
  output [31:0] View2
);

  wire demultiplexer_1_out0, demultiplexer_1_out1;
  wire [31:0] banco_32bit_1_viewreg1, banco_32bit_1_viewreg2, banco_32bit_2_viewreg1, banco_32bit_2_viewreg2;

  Demultiplexer #(.enable("false")) demultiplexer_1 (
    .out0(demultiplexer_1_out0), .out1(demultiplexer_1_out1), .in(CLK), .sel(CONTEXTO));
  banco_32bit banco_32bit_1 (
    .CLK(demultiplexer_1_out0), .Data(DATAIN), .Reset(RESET), .WReg(WReg), .Reg1(Reg1), .Reg2(Reg2),
    .ViewReg1(banco_32bit_1_viewreg1), .ViewReg2(banco_32bit_1_viewreg2));  // open: Zero1, Zero2
  banco_32bit banco_32bit_2 (
    .CLK(demultiplexer_1_out1), .Data(DATAIN), .Reset(RESET), .WReg(WReg), .Reg1(Reg1), .Reg2(Reg2),
    .ViewReg1(banco_32bit_2_viewreg1), .ViewReg2(banco_32bit_2_viewreg2));  // open: Zero1, Zero2
  Multiplexer #(.width(32), .enable("false")) multiplexer_1 (
    .in0(banco_32bit_1_viewreg1), .in1(banco_32bit_2_viewreg1), .out(View1), .sel(CONTEXTO));
  Multiplexer #(.width(32), .enable("false")) multiplexer_2 (
    .in0(banco_32bit_1_viewreg2), .in1(banco_32bit_2_viewreg2), .out(View2), .sel(CONTEXTO));
endmodule
