// Logisim project introducao.circ as structural Verilog: 4 circuits, main circuit main
module main (
  input  in_1,
  input  in_2,
  output out_3,
  output out_4
);

  and and_1 (out_3, in_1, in_2);
  or or_1 (out_4, in_1, in_2);

  // Notes on the sheet:
  //   Introdução ao Logisim
endmodule

module mux2 (
  input  A,
  input  B,
  input  Select,
  output Output
);

  wire and_1_out, and_2_out;

  and and_1 (and_1_out, A, ~Select);  // AND_Gate
  and and_2 (and_2_out, B, Select);
  or or_1 (Output, and_1_out, and_2_out);
endmodule

module mux4_with_mux2 (
  input  _0,
  input  _1,
  input  _2,
  input  _3,
  input  Select1,
  input  Select2,
  output Output
);

  wire mux2_1_output, mux2_2_output;

  mux2 mux2_1 (.A(_0), .B(_1), .Select(Select1), .Output(mux2_1_output));
  mux2 mux2_2 (.A(_2), .B(_3), .Select(Select1), .Output(mux2_2_output));
  mux2 mux2_3 (.A(mux2_1_output), .B(mux2_2_output), .Select(Select2), .Output(Output));
endmodule

module mux4 (
  input  in_1,
  input  in_2,
  input  in_3,
  input  in_4,
  input  in_5,
  input  in_6,
  output out_7
);

  wire and_1_out, and_2_out, and_3_out, and_4_out;

  and and_1 (and_1_out, in_1, ~in_5, ~in_6);  // AND_Gate
  and and_2 (and_2_out, in_2, ~in_5, in_6);  // AND_Gate
  and and_3 (and_3_out, in_3, in_5, ~in_6);  // AND_Gate
  and and_4 (and_4_out, in_4, in_5, in_6);
  or or_1 (out_7, and_1_out, and_2_out, and_3_out, and_4_out);
endmodule
