// Logisim project mux.circ as structural Verilog: 4 circuits, main circuit mux_8:1
module mux_8_1 (
  input  _0,
  input  _1,
  input  _2,
  input  _3,
  input  _4,
  input  _5,
  input  _6,
  input  _7,
  input  S_prime_2,
  input  S_prime_1,
  input  S_prime_0,
  output Output
);

  wire and_1_out, and_2_out, and_3_out, and_4_out, and_5_out, and_6_out, and_7_out, and_8_out;

  and and_1 (and_1_out, _0, ~S_prime_2, ~S_prime_1, ~S_prime_0);  // AND_Gate
  and and_2 (and_2_out, _1, ~S_prime_2, ~S_prime_1, S_prime_0);  // AND_Gate
  and and_3 (and_3_out, _2, ~S_prime_2, S_prime_1, ~S_prime_0);  // AND_Gate
  and and_4 (and_4_out, _3, ~S_prime_2, S_prime_1, S_prime_0);  // AND_Gate
  and and_5 (and_5_out, _4, S_prime_2, ~S_prime_1, ~S_prime_0);  // AND_Gate
  and and_6 (and_6_out, _5, S_prime_2, ~S_prime_1, S_prime_0);  // AND_Gate
  and and_7 (and_7_out, _6, S_prime_2, S_prime_1, ~S_prime_0);  // AND_Gate
  and and_8 (and_8_out, _7, S_prime_2, S_prime_1, S_prime_0);
  or or_1 (Output, and_1_out, and_2_out, and_3_out, and_4_out, and_5_out, and_6_out, and_7_out, and_8_out);
endmodule

module mux_16_1 (
  input  _0,
  input  _1,
  input  _2,
  input  _3,
  input  _4,
  input  _5,
  input  _6,
  input  _7,
  input  _8,
  input  _9,
  input  _10,
  input  _11,
  input  _12,
  input  _13,
  input  _14,
  input  _15,
  input  S_prime_3,
  input  S_prime_2,
  input  S_prime_1,
  input  S_prime_0,
  output Output
);

  wire mux_8_1_1_output, mux_8_1_2_output;

  mux_8_1 mux_8_1_1 (
    ._0(_0), ._1(_1), ._2(_2), ._3(_3), ._4(_4), ._5(_5), ._6(_6), ._7(_7), .S_prime_2(S_prime_2),
    .S_prime_1(S_prime_1), .S_prime_0(S_prime_0), .Output(mux_8_1_1_output));
  mux_8_1 mux_8_1_2 (
    ._0(_8), ._1(_9), ._2(_10), ._3(_11), ._4(_12), ._5(_13), ._6(_14), ._7(_15), .S_prime_2(S_prime_2),
    .S_prime_1(S_prime_1), .S_prime_0(S_prime_0), .Output(mux_8_1_2_output));
  mux_2_1 mux_2_1_1 (.A(mux_8_1_1_output), .B(mux_8_1_2_output), .S_prime_0(S_prime_3), .Output(Output));
endmodule

module mux_2_1 (
  input  A,
  input  B,
  input  S_prime_0,
  output Output
);

  wire and_1_out, and_2_out;

  and and_1 (and_1_out, A, ~S_prime_0);  // AND_Gate
  and and_2 (and_2_out, B, S_prime_0);
  or or_1 (Output, and_1_out, and_2_out);
endmodule

module mux_32_1 (
  input  _0,
  input  _1,
  input  _2,
  input  _3,
  input  _4,
  input  _5,
  input  _6,
  input  _7,
  input  _8,
  input  _9,
  input  _10,
  input  _11,
  input  _12,
  input  _13,
  input  _14,
  input  _15,
  input  _16,
  input  _17,
  input  _18,
  input  _19,
  input  _20,
  input  _21,
  input  _22,
  input  _23,
  input  _24,
  input  _25,
  input  _26,
  input  _27,
  input  _28,
  input  _29,
  input  _30,
  input  _31,
  input  S_prime_4,
  input  S_prime_3,
  input  S_prime_2,
  input  S_prime_1,
  input  S_prime_0,
  output Output
);

  wire mux_16_1_1_output, mux_16_1_2_output;

  mux_16_1 mux_16_1_1 (
    ._0(_0), ._1(_1), ._2(_2), ._3(_3), ._4(_4), ._5(_5), ._6(_6), ._7(_7), ._8(_8), ._9(_9), ._10(_10),
    ._11(_11), ._12(_12), ._13(_13), ._14(_14), ._15(_15), .S_prime_3(S_prime_3), .S_prime_2(S_prime_2),
    .S_prime_1(S_prime_1), .S_prime_0(S_prime_0), .Output(mux_16_1_1_output));
  mux_16_1 mux_16_1_2 (
    ._0(_16), ._1(_17), ._2(_18), ._3(_19), ._4(_20), ._5(_21), ._6(_22), ._7(_23), ._8(_24), ._9(_25),
    ._10(_26), ._11(_27), ._12(_28), ._13(_29), ._14(_30), ._15(_31), .S_prime_3(S_prime_3),
    .S_prime_2(S_prime_2), .S_prime_1(S_prime_1), .S_prime_0(S_prime_0), .Output(mux_16_1_2_output));
  mux_2_1 mux_2_1_1 (.A(mux_16_1_1_output), .B(mux_16_1_2_output), .S_prime_0(S_prime_4), .Output(Output));
endmodule
