// Logisim project ula-32bit.circ as structural Verilog: 20 circuits, main circuit ula
module ula (
  input  [31:0] A,
  input  [31:0] B,
  input  [4:0] ULA_OpCode,
  output Zero,
  output [31:0] Out
);

  wire sla_a_d_1_shift, sla_b_d_1_shift, sll_a_d_1_shift, sll_b_d_1_shift, sra_a_d_1_shift, sra_b_d_1_shift,
       srl_a_d_1_shift, srl_b_d_1_shift, ula_cell_1_c_prime_out, ula_cell_3_c_prime_out,
       ula_cell_4_c_prime_out, ula_cell_5_c_prime_out, ula_cell_6_c_prime_out, ula_cell_7_c_prime_out,
       ula_cell_8_c_prime_out, ula_cell_9_c_prime_out, ula_cell_10_c_prime_out, ula_cell_11_c_prime_out,
       ula_cell_12_c_prime_out, ula_cell_13_c_prime_out, ula_cell_14_c_prime_out, ula_cell_15_c_prime_out,
       ula_cell_16_c_prime_out, ula_cell_17_c_prime_out, ula_cell_18_c_prime_out, ula_cell_19_c_prime_out,
       ula_cell_20_c_prime_out, ula_cell_21_c_prime_out, ula_cell_22_c_prime_out, ula_cell_23_c_prime_out,
       ula_cell_24_c_prime_out, ula_cell_25_c_prime_out, ula_cell_26_c_prime_out, ula_cell_27_c_prime_out,
       ula_cell_28_c_prime_out, ula_cell_29_c_prime_out, ula_cell_30_c_prime_out, ula_cell_31_c_prime_out,
       ula_cell_32_c_prime_out;
  wire [31:0] shift_left_arith_1_out, shift_left_arith_2_out, shift_left_logical_1_out,
       shift_left_logical_2_out, shift_right_arith_1_out, shift_right_arith_2_out, shift_right_logical_1_out,
       shift_right_logical_2_out;

  shift_left_logical shift_left_logical_1 (.In(A), .Out(shift_left_logical_1_out), .Shift(sll_a_d_1_shift));
  shift_right_logical shift_right_logical_1 (
    .In(shift_left_logical_1_out), .Out(shift_right_logical_1_out), .Shift(srl_a_d_1_shift));
  sll_a_d sll_a_d_1 (.Shift(sll_a_d_1_shift), .OpCode(ULA_OpCode));
  srl_a_d srl_a_d_1 (.Shift(srl_a_d_1_shift), .UlaOpCode(ULA_OpCode));
  shift_left_logical shift_left_logical_2 (.In(B), .Out(shift_left_logical_2_out), .Shift(sll_b_d_1_shift));
  shift_right_logical shift_right_logical_2 (
    .In(shift_left_logical_2_out), .Out(shift_right_logical_2_out), .Shift(srl_b_d_1_shift));
  srl_b_d srl_b_d_1 (.Shift(srl_b_d_1_shift), .UlaOpCode(ULA_OpCode));
  sll_b_d sll_b_d_1 (.Shift(sll_b_d_1_shift), .UlaOpCode(ULA_OpCode));
  shift_right_arith shift_right_arith_1 (
    .In(shift_left_arith_1_out), .Out(shift_right_arith_1_out), .Shift(sra_a_d_1_shift));
  shift_left_arith shift_left_arith_1 (
    .In(shift_right_logical_1_out), .Out(shift_left_arith_1_out), .Shift(sla_a_d_1_shift));
  sla_a_d sla_a_d_1 (.Shift(sla_a_d_1_shift), .UlaOpCode(ULA_OpCode));
  sra_a_d sra_a_d_1 (.Shift(sra_a_d_1_shift), .UlaOpCode(ULA_OpCode));
  shift_right_arith shift_right_arith_2 (
    .In(shift_left_arith_2_out), .Out(shift_right_arith_2_out), .Shift(sra_b_d_1_shift));
  shift_left_arith shift_left_arith_2 (
    .In(shift_right_logical_2_out), .Out(shift_left_arith_2_out), .Shift(sla_b_d_1_shift));
  sla_b_d sla_b_d_1 (.Shift(sla_b_d_1_shift), .UlaOpCode(ULA_OpCode));
  sra_b_d sra_b_d_1 (.Shift(sra_b_d_1_shift), .UlaOpCode(ULA_OpCode));
  ula_cell ula_cell_1 (
    .C_prime_out(ula_cell_1_c_prime_out), .B(shift_right_arith_2_out[30]), .A(shift_right_arith_1_out[30]),
    .OpCode(ULA_OpCode), .Out(Out[30]), .C_prime_in(ula_cell_3_c_prime_out));
  ula_cell ula_cell_2 (
    .B(shift_right_arith_2_out[31]), .A(shift_right_arith_1_out[31]), .OpCode(ULA_OpCode), .Out(Out[31]),
    .C_prime_in(ula_cell_1_c_prime_out));  // open: C_prime_out
  ula_cell ula_cell_3 (
    .C_prime_out(ula_cell_3_c_prime_out), .B(shift_right_arith_2_out[29]), .A(shift_right_arith_1_out[29]),
    .OpCode(ULA_OpCode), .Out(Out[29]), .C_prime_in(ula_cell_4_c_prime_out));
  ula_cell ula_cell_4 (
    .C_prime_out(ula_cell_4_c_prime_out), .B(shift_right_arith_2_out[28]), .A(shift_right_arith_1_out[28]),
    .OpCode(ULA_OpCode), .Out(Out[28]), .C_prime_in(ula_cell_5_c_prime_out));
  ula_cell ula_cell_5 (
    .C_prime_out(ula_cell_5_c_prime_out), .B(shift_right_arith_2_out[27]), .A(shift_right_arith_1_out[27]),
    .OpCode(ULA_OpCode), .Out(Out[27]), .C_prime_in(ula_cell_6_c_prime_out));
  ula_cell ula_cell_6 (
    .C_prime_out(ula_cell_6_c_prime_out), .B(shift_right_arith_2_out[26]), .A(shift_right_arith_1_out[26]),
    .OpCode(ULA_OpCode), .Out(Out[26]), .C_prime_in(ula_cell_7_c_prime_out));
  ula_cell ula_cell_7 (
    .C_prime_out(ula_cell_7_c_prime_out), .B(shift_right_arith_2_out[25]), .A(shift_right_arith_1_out[25]),
    .OpCode(ULA_OpCode), .Out(Out[25]), .C_prime_in(ula_cell_8_c_prime_out));
  ula_cell ula_cell_8 (
    .C_prime_out(ula_cell_8_c_prime_out), .B(shift_right_arith_2_out[24]), .A(shift_right_arith_1_out[24]),
    .OpCode(ULA_OpCode), .Out(Out[24]), .C_prime_in(ula_cell_9_c_prime_out));
  ula_cell ula_cell_9 (
    .C_prime_out(ula_cell_9_c_prime_out), .B(shift_right_arith_2_out[23]), .A(shift_right_arith_1_out[23]),
    .OpCode(ULA_OpCode), .Out(Out[23]), .C_prime_in(ula_cell_10_c_prime_out));
  ula_cell ula_cell_10 (
    .C_prime_out(ula_cell_10_c_prime_out), .B(shift_right_arith_2_out[22]), .A(shift_right_arith_1_out[22]),
    .OpCode(ULA_OpCode), .Out(Out[22]), .C_prime_in(ula_cell_11_c_prime_out));
  ula_cell ula_cell_11 (
    .C_prime_out(ula_cell_11_c_prime_out), .B(shift_right_arith_2_out[21]), .A(shift_right_arith_1_out[21]),
    .OpCode(ULA_OpCode), .Out(Out[21]), .C_prime_in(ula_cell_13_c_prime_out));
  ula_cell ula_cell_12 (
    .C_prime_out(ula_cell_12_c_prime_out), .B(shift_right_arith_2_out[19]), .A(shift_right_arith_1_out[19]),
    .OpCode(ULA_OpCode), .Out(Out[19]), .C_prime_in(ula_cell_14_c_prime_out));
  ula_cell ula_cell_13 (
    .C_prime_out(ula_cell_13_c_prime_out), .B(shift_right_arith_2_out[20]), .A(shift_right_arith_1_out[20]),
    .OpCode(ULA_OpCode), .Out(Out[20]), .C_prime_in(ula_cell_12_c_prime_out));
  ula_cell ula_cell_14 (
    .C_prime_out(ula_cell_14_c_prime_out), .B(shift_right_arith_2_out[18]), .A(shift_right_arith_1_out[18]),
    .OpCode(ULA_OpCode), .Out(Out[18]), .C_prime_in(ula_cell_16_c_prime_out));
  ula_cell ula_cell_15 (
    .C_prime_out(ula_cell_15_c_prime_out), .B(shift_right_arith_2_out[16]), .A(shift_right_arith_1_out[16]),
    .OpCode(ULA_OpCode), .Out(Out[16]), .C_prime_in(ula_cell_17_c_prime_out));
  ula_cell ula_cell_16 (
    .C_prime_out(ula_cell_16_c_prime_out), .B(shift_right_arith_2_out[17]), .A(shift_right_arith_1_out[17]),
    .OpCode(ULA_OpCode), .Out(Out[17]), .C_prime_in(ula_cell_15_c_prime_out));
  ula_cell ula_cell_17 (
    .C_prime_out(ula_cell_17_c_prime_out), .B(shift_right_arith_2_out[15]), .A(shift_right_arith_1_out[15]),
    .OpCode(ULA_OpCode), .Out(Out[15]), .C_prime_in(ula_cell_18_c_prime_out));
  ula_cell ula_cell_18 (
    .C_prime_out(ula_cell_18_c_prime_out), .B(shift_right_arith_2_out[14]), .A(shift_right_arith_1_out[14]),
    .OpCode(ULA_OpCode), .Out(Out[14]), .C_prime_in(ula_cell_19_c_prime_out));
  ula_cell ula_cell_19 (
    .C_prime_out(ula_cell_19_c_prime_out), .B(shift_right_arith_2_out[13]), .A(shift_right_arith_1_out[13]),
    .OpCode(ULA_OpCode), .Out(Out[13]), .C_prime_in(ula_cell_20_c_prime_out));
  ula_cell ula_cell_20 (
    .C_prime_out(ula_cell_20_c_prime_out), .B(shift_right_arith_2_out[12]), .A(shift_right_arith_1_out[12]),
    .OpCode(ULA_OpCode), .Out(Out[12]), .C_prime_in(ula_cell_21_c_prime_out));
  ula_cell ula_cell_21 (
    .C_prime_out(ula_cell_21_c_prime_out), .B(shift_right_arith_2_out[11]), .A(shift_right_arith_1_out[11]),
    .OpCode(ULA_OpCode), .Out(Out[11]), .C_prime_in(ula_cell_22_c_prime_out));
  ula_cell ula_cell_22 (
    .C_prime_out(ula_cell_22_c_prime_out), .B(shift_right_arith_2_out[10]), .A(shift_right_arith_1_out[10]),
    .OpCode(ULA_OpCode), .Out(Out[10]), .C_prime_in(ula_cell_24_c_prime_out));
  ula_cell ula_cell_23 (
    .C_prime_out(ula_cell_23_c_prime_out), .B(shift_right_arith_2_out[8]), .A(shift_right_arith_1_out[8]),
    .OpCode(ULA_OpCode), .Out(Out[8]), .C_prime_in(ula_cell_25_c_prime_out));
  ula_cell ula_cell_24 (
    .C_prime_out(ula_cell_24_c_prime_out), .B(shift_right_arith_2_out[9]), .A(shift_right_arith_1_out[9]),
    .OpCode(ULA_OpCode), .Out(Out[9]), .C_prime_in(ula_cell_23_c_prime_out));
  ula_cell ula_cell_25 (
    .C_prime_out(ula_cell_25_c_prime_out), .B(shift_right_arith_2_out[7]), .A(shift_right_arith_1_out[7]),
    .OpCode(ULA_OpCode), .Out(Out[7]), .C_prime_in(ula_cell_26_c_prime_out));
  ula_cell ula_cell_26 (
    .C_prime_out(ula_cell_26_c_prime_out), .B(shift_right_arith_2_out[6]), .A(shift_right_arith_1_out[6]),
    .OpCode(ULA_OpCode), .Out(Out[6]), .C_prime_in(ula_cell_27_c_prime_out));
  ula_cell ula_cell_27 (
    .C_prime_out(ula_cell_27_c_prime_out), .B(shift_right_arith_2_out[5]), .A(shift_right_arith_1_out[5]),
    .OpCode(ULA_OpCode), .Out(Out[5]), .C_prime_in(ula_cell_29_c_prime_out));
  ula_cell ula_cell_28 (
    .C_prime_out(ula_cell_28_c_prime_out), .B(shift_right_arith_2_out[3]), .A(shift_right_arith_1_out[3]),
    .OpCode(ULA_OpCode), .Out(Out[3]), .C_prime_in(ula_cell_30_c_prime_out));
  ula_cell ula_cell_29 (
    .C_prime_out(ula_cell_29_c_prime_out), .B(shift_right_arith_2_out[4]), .A(shift_right_arith_1_out[4]),
    .OpCode(ULA_OpCode), .Out(Out[4]), .C_prime_in(ula_cell_28_c_prime_out));
  ula_cell ula_cell_30 (
    .C_prime_out(ula_cell_30_c_prime_out), .B(shift_right_arith_2_out[2]), .A(shift_right_arith_1_out[2]),
    .OpCode(ULA_OpCode), .Out(Out[2]), .C_prime_in(ula_cell_32_c_prime_out));
  ula_cell ula_cell_31 (
    .C_prime_out(ula_cell_31_c_prime_out), .B(shift_right_arith_2_out[0]), .A(shift_right_arith_1_out[0]),
    .OpCode(ULA_OpCode), .Out(Out[0]), .C_prime_in(1'b0));
  ula_cell ula_cell_32 (
    .C_prime_out(ula_cell_32_c_prime_out), .B(shift_right_arith_2_out[1]), .A(shift_right_arith_1_out[1]),
    .OpCode(ULA_OpCode), .Out(Out[1]), .C_prime_in(ula_cell_31_c_prime_out));
  and and_1 (Zero, ~Out[31], ~Out[30], ~Out[29], ~Out[28], ~Out[27], ~Out[26], ~Out[25], ~Out[24], ~Out[23], ~Out[22], ~Out[21], ~Out[20], ~Out[19], ~Out[18], ~Out[17], ~Out[16], ~Out[15], ~Out[14], ~Out[13], ~Out[12], ~Out[11], ~Out[10], ~Out[9], ~Out[8], ~Out[7], ~Out[6], ~Out[5], ~Out[4], ~Out[3], ~Out[2], ~Out[1], ~Out[0]);  // AND_Gate
  // NOT_Gate not_1 is placed but not wired
endmodule

module teste (
  input  [31:0] A,
  input  [31:0] B,
  input  [4:0] ULA_OpCode,
  output Zero,
  output [31:0] Out
);

  ula ula_1 (.A(A), .B(B), .Out(Out), .ULA_OpCode(ULA_OpCode), .Zero(Zero));

  // Notes on the sheet:
  //   00000 - AND
  //   00001 - OR
  //   00010- ADD
  //   00011 - XOR
  //   00100 - SLL A
  //   00101 - SLL B
  //   00110 - SRL A
  //   00111 - SRL B
  //   01000 - SLA A 
  //   01001 - SLA B
  //   01010 - SRA A 
  //   01011 - SRA B
endmodule

module adder (
  input  C_prime_in,
  input  A,
  input  B,
  output Sum,
  output C_prime_out
);

  wire and_1_out, and_2_out, xor_1_out;

  xor xor_1 (xor_1_out, A, B);
  xor xor_2 (Sum, xor_1_out, C_prime_in);
  and and_1 (and_1_out, xor_1_out, C_prime_in);
  and and_2 (and_2_out, A, B);
  or or_1 (C_prime_out, and_1_out, and_2_out);
endmodule

module mux_4_1 (
  input  _0,
  input  _1,
  input  _2,
  input  _3,
  input  [1:0] in_5,
  output Out
);

  wire and_1_out, and_2_out, and_3_out, and_4_out;

  and and_1 (and_1_out, _0, ~in_5[1], ~in_5[0]);  // AND_Gate
  and and_2 (and_2_out, _1, ~in_5[1], in_5[0]);  // AND_Gate
  and and_3 (and_3_out, _2, in_5[1], ~in_5[0]);  // AND_Gate
  and and_4 (and_4_out, _3, in_5[1], in_5[0]);
  or or_1 (Out, and_1_out, and_2_out, and_3_out, and_4_out);
endmodule

module mux_8_1 (
  input  o,
  input  _1,
  input  _2,
  input  _3,
  input  _4,
  input  _5,
  input  _6,
  input  _7,
  input  [2:0] Select,
  output Out
);

  wire and_1_out, and_2_out, and_3_out, and_4_out, and_5_out, and_6_out, and_7_out, and_8_out;

  and and_1 (and_1_out, o, ~Select[2], ~Select[1], ~Select[0]);  // AND_Gate
  and and_2 (and_2_out, _1, ~Select[2], ~Select[1], Select[0]);  // AND_Gate
  and and_3 (and_3_out, _2, ~Select[2], Select[1], ~Select[0]);  // AND_Gate
  and and_4 (and_4_out, _3, ~Select[2], Select[1], Select[0]);  // AND_Gate
  and and_5 (and_5_out, _4, Select[2], ~Select[1], ~Select[0]);  // AND_Gate
  and and_6 (and_6_out, _5, Select[2], ~Select[1], Select[0]);  // AND_Gate
  and and_7 (and_7_out, _6, Select[2], Select[1], ~Select[0]);  // AND_Gate
  and and_8 (and_8_out, _7, Select[2], Select[1], Select[0]);
  or or_1 (Out, and_1_out, and_2_out, and_3_out, and_4_out, and_5_out, and_6_out, and_7_out, and_8_out);
endmodule

module mux_32_1 (
  input  o,
  input  _1,
  input  _2,
  input  _3,
  input  _4,
  input  _5,
  input  _6,
  input  _7,
  input  _8,
  input  _9,
  input  _10,
  input  _11,
  input  _12,
  input  _13,
  input  _14,
  input  _15,
  input  _16,
  input  _17,
  input  _18,
  input  _19,
  input  _20,
  input  _21,
  input  _22,
  input  _23,
  input  _24,
  input  _25,
  input  _26,
  input  _27,
  input  _28,
  input  _29,
  input  _30,
  input  _31,
  input  [4:0] Select,
  output Out
);

  wire mux_8_1_1_out, mux_8_1_2_out, mux_8_1_3_out, mux_8_1_4_out;

  mux_8_1 mux_8_1_1 (
    .o(o), ._1(_1), ._2(_2), ._3(_3), ._4(_4), ._5(_5), ._6(_6), ._7(_7), .Out(mux_8_1_1_out),
    .Select(Select[2:0]));
  mux_8_1 mux_8_1_2 (
    .o(_8), ._1(_9), ._2(_10), ._3(_11), ._4(_12), ._5(_13), ._6(_14), ._7(_15), .Out(mux_8_1_2_out),
    .Select(Select[2:0]));
  mux_4_1 mux_4_1_1 (
    ._0(mux_8_1_1_out), ._1(mux_8_1_2_out), ._2(mux_8_1_3_out), ._3(mux_8_1_4_out), .Out(Out),
    .in_5(Select[4:3]));
  mux_8_1 mux_8_1_3 (
    .o(_16), ._1(_17), ._2(_18), ._3(_19), ._4(_20), ._5(_21), ._6(_22), ._7(_23), .Out(mux_8_1_3_out),
    .Select(Select[2:0]));
  mux_8_1 mux_8_1_4 (
    .o(_24), ._1(_25), ._2(_26), ._3(_27), ._4(_28), ._5(_29), ._6(_30), ._7(_31), .Out(mux_8_1_4_out),
    .Select(Select[2:0]));
endmodule

module mux_2_32 (
  input  [31:0] A,
  input  [31:0] B,
  input  SEL,
  output [31:0] out_4
);

  wire [31:0] and_1_out, and_2_out;

  assign and_1_out = A & ~{32{SEL}};  // AND_Gate and_1, 32 bits wide
  assign and_2_out = B & {32{SEL}};  // AND_Gate and_2, 32 bits wide
  assign out_4 = and_1_out | and_2_out;  // OR_Gate or_1, 32 bits wide
endmodule

module ula_cell (
  input  B,
  input  A,
  input  C_prime_in,
  input  [4:0] OpCode,
  output C_prime_out,
  output Out
);

  wire adder_1_sum, and_1_out, nand_1_out, or_1_out, xor_1_out;

  and and_1 (and_1_out, A, B);
  or or_1 (or_1_out, A, B);
  adder adder_1 (.A(A), .B(B), .Sum(adder_1_sum), .C_prime_in(C_prime_in), .C_prime_out(C_prime_out));
  xor xor_1 (xor_1_out, A, B);
  nand nand_1 (nand_1_out, ~A, B);  // NAND_Gate
  mux_32_1 mux_32_1_1 (
    .o(and_1_out), ._1(or_1_out), ._2(adder_1_sum), ._3(xor_1_out), ._4(A), ._5(B), ._6(A), ._7(B), ._8(A),
    ._9(B), ._10(A), ._11(B), ._31(nand_1_out), .Out(Out), .Select(OpCode));  // open: _12, _13, _14, _15, _16, _17, _18, _19, _20, _21, _22, _23, _24, _25, _26, _27, _28, _29, _30

  // Notes on the sheet:
  //   00000 - AND
  //   00001 - OR
  //   00010- ADD
  //   00011 - XOR
  //   00100 - SLL A
  //   00101 - SLL B
  //   00110 - SRL A
  //   00111 - SRL B
  //   01000 - SLA A 
  //   01001 - SLA B
  //   01010 - SRA A 
  //   01011 - SRA B
  //   11111 - ~AB
endmodule

module shift_left_logical (
  input  [31:0] In,
  input  Shift,
  output [31:0] Out
);

  mux_2_32 mux_2_32_1 (.A(In), .B({In[30:0], 1'b0}), .out_4(Out), .SEL(Shift));
endmodule

module shift_left_arith (
  input  [31:0] In,
  input  Shift,
  output [31:0] Out
);

  mux_2_32 mux_2_32_1 (.A(In), .B({In[30:0], In[0]}), .out_4(Out), .SEL(Shift));
endmodule

module shift_right_logical (
  input  [31:0] In,
  input  Shift,
  output [31:0] Out
);

  mux_2_32 mux_2_32_1 (.A(In), .B({1'b0, In[31:1]}), .out_4(Out), .SEL(Shift));
endmodule

module shift_right_arith (
  input  [31:0] In,
  input  Shift,
  output [31:0] Out
);

  mux_2_32 mux_2_32_1 (.A(In), .B({{2{In[31]}}, In[30:1]}), .out_4(Out), .SEL(Shift));
endmodule

module sll_a_d (
  input  [4:0] OpCode,
  output Shift
);

  and and_1 (Shift, ~OpCode[4], ~OpCode[3], OpCode[2], ~OpCode[1], ~OpCode[0]);  // AND_Gate
endmodule

module sll_b_d (
  input  [4:0] UlaOpCode,
  output Shift
);

  and and_1 (Shift, ~UlaOpCode[4], ~UlaOpCode[3], UlaOpCode[2], ~UlaOpCode[1], UlaOpCode[0]);  // AND_Gate
endmodule

module srl_a_d (
  input  [4:0] UlaOpCode,
  output Shift
);

  and and_1 (Shift, ~UlaOpCode[4], ~UlaOpCode[3], UlaOpCode[2], UlaOpCode[1], ~UlaOpCode[0]);  // AND_Gate
endmodule

module srl_b_d (
  input  [4:0] UlaOpCode,
  output Shift
);

  and and_1 (Shift, ~UlaOpCode[4], ~UlaOpCode[3], UlaOpCode[2], UlaOpCode[1], UlaOpCode[0]);  // AND_Gate
endmodule

module sla_a_d (
  input  [4:0] UlaOpCode,
  output Shift
);

  and and_1 (Shift, ~UlaOpCode[4], UlaOpCode[3], ~UlaOpCode[2], ~UlaOpCode[1], ~UlaOpCode[0]);  // AND_Gate
endmodule

module sla_b_d (
  input  [4:0] UlaOpCode,
  output Shift
);

  and and_1 (Shift, ~UlaOpCode[4], UlaOpCode[3], ~UlaOpCode[2], ~UlaOpCode[1], UlaOpCode[0]);  // AND_Gate
endmodule

module sra_a_d (
  input  [4:0] UlaOpCode,
  output Shift
);

  and and_1 (Shift, ~UlaOpCode[4], UlaOpCode[3], ~UlaOpCode[2], UlaOpCode[1], ~UlaOpCode[0]);  // AND_Gate
endmodule

module sra_b_d (
  input  [4:0] UlaOpCode,
  output Shift
);

  and and_1 (Shift, ~UlaOpCode[4], UlaOpCode[3], ~UlaOpCode[2], UlaOpCode[1], UlaOpCode[0]);  // AND_Gate
endmodule
