// Logisim project ula.circ as structural Verilog: 7 circuits, main circuit mux_4:1
module mux_4_1 (
  input  _0,
  input  _1,
  input  _2,
  input  _3,
  input  SEL_prime_1,
  input  SEL_prime_0,
  output Output
);

  wire and_1_out, and_2_out, and_3_out, and_4_out;

  and and_1 (and_1_out, _0, ~SEL_prime_1, ~SEL_prime_0);  // AND_Gate
  and and_2 (and_2_out, _1, ~SEL_prime_1, SEL_prime_0);  // AND_Gate
  and and_3 (and_3_out, _2, SEL_prime_1, ~SEL_prime_0);  // AND_Gate
  and and_4 (and_4_out, _3, SEL_prime_1, SEL_prime_0);
  or or_1 (Output, and_1_out, and_2_out, and_3_out, and_4_out);
endmodule

module adder (
  input  A,
  input  B,
  input  Carry_In,
  output Sum,
  output Carry_Out
);

  wire AB_out, AC_out, BC_out, xor_1_out;

  xor xor_1 (xor_1_out, A, B);
  and AB (AB_out, A, B);
  and BC (BC_out, B, Carry_In);
  and AC (AC_out, A, Carry_In);
  xor xor_2 (Sum, xor_1_out, Carry_In);
  or or_1 (Carry_Out, AB_out, BC_out, AC_out);

  // Notes on the sheet:
  //   XOR -> eXclusive OR
endmodule

module ula_cell (
  input  B,
  input  A,
  input  C_prime_in,
  input  Sel_prime_1,
  input  Sel_prime_0,
  output Result,
  output C_prime_Out
);

  wire and_1_out, or_1_out, undriven, xor_1_out;

  and and_1 (and_1_out, A, B);
  or or_1 (or_1_out, A, B);
  xor xor_1 (xor_1_out, A, B);
  adder adder_1 (.A(A), .B(B), .Carry_In(C_prime_in), .Sum(C_prime_Out));  // open: Carry_Out
  mux_4_1 mux_4_1_1 (
    ._0(and_1_out), ._1(or_1_out), ._2(xor_1_out), ._3(undriven), .SEL_prime_1(Sel_prime_1),
    .SEL_prime_0(Sel_prime_0), .Output(Result));
endmodule

module ula (
  input  [3:0] A,
  input  [3:0] B,
  input  [1:0] ULAOpCode,
  output [3:0] Result
);

  wire ula_cell_1_p5, ula_cell_2_result, ula_cell_3_result, ula_cell_4_result;

  // ula_cell ula_cell_1: pin names not known; wires that end beside it: B[3], ULAOpCode, A[3], Result[3], ula_cell_1_p5
  ula_cell ula_cell_2 (
    .C_prime_in(ula_cell_1_p5), .B(B[2]), .A(A[2]), .Sel_prime_1(ULAOpCode[0]), .Sel_prime_0(Result[2]),
    .Result(ula_cell_2_result));  // open: C_prime_Out
  ula_cell ula_cell_3 (
    .C_prime_in(ula_cell_2_result), .B(B[1]), .A(A[1]), .Sel_prime_1(ULAOpCode[0]), .Sel_prime_0(Result[1]),
    .Result(ula_cell_3_result));  // open: C_prime_Out
  ula_cell ula_cell_4 (
    .C_prime_in(ula_cell_3_result), .B(B[0]), .A(A[0]), .Sel_prime_1(ULAOpCode[0]), .Sel_prime_0(Result[0]),
    .Result(ula_cell_4_result));  // open: C_prime_Out
  // Pins of 1 and 2 bits meet at ULAOpCode
  // also tied to GND on the sheet: ula_cell_4_result

  // Notes on the sheet:
  //   00 = AND
  //   01 = OR
  //   10 = SOMA
  //   11 = XOR
endmodule

module shift_letf_logical_1bit (
  input  [3:0] Input,
  output [3:0] Out
);


  assign Out = {Input[2:0], 1'b0};
endmodule

module shift_rigtht_logical_1bit (
  input  [3:0] Input,
  input  in_2,
  output [3:0] Out
);

  Multiplexer multiplexer_1 (.in0(Input[0]), .in1(Input[1]), .out(Out[0]), .sel(in_2));  // open: en
  // Pins of 1 and 4 bits meet at Input
  // Pins of 1 and 4 bits meet at {{2{Input[3]}}, Input[2:1]}
  // Pins of 1 and 4 bits meet at Out
endmodule

module SLLDetect (
  input  [2:0] ULAOpCode,
  output SLL
);

  and and_1 (SLL, ~ULAOpCode[0], ~ULAOpCode[1], ULAOpCode[2]);  // AND_Gate
endmodule
