// Logisim project unidade-logica-aritimetica.circ as structural Verilog: 8 circuits, main circuit ula
module ula (
  input  [3:0] A,
  input  [3:0] B,
  input  in_3,
  input  in_4,
  input  [2:0] ULAOpCode,
  output [3:0] Result
);

  wire slldetect_1_sll, ula_cell_2_c_prime_out, ula_cell_3_c_prime_out, ula_cell_4_c_prime_out;
  wire [3:0] shift_letf_logical_1bit_1_out, shift_right_arith_1bit_1_out, shift_rigtht_logical_1bit_1_out;

  shift_letf_logical_1bit shift_letf_logical_1bit_1 (
    .In(B), .Shift(slldetect_1_sll), .Out(shift_letf_logical_1bit_1_out));
  SLLDetect slldetect_1 (.ULAOpCode(ULAOpCode), .SLL(slldetect_1_sll));
  shift_rigtht_logical_1bit shift_rigtht_logical_1bit_1 (
    .In(shift_letf_logical_1bit_1_out), .Shift(in_3), .Out(shift_rigtht_logical_1bit_1_out));
  shift_right_arith_1bit shift_right_arith_1bit_1 (
    .In(shift_rigtht_logical_1bit_1_out), .Shift(in_4), .Out(shift_right_arith_1bit_1_out));
  ula_cell ula_cell_1 (
    .B(shift_right_arith_1bit_1_out[3]), .A(A[3]), .OpCode(ULAOpCode), .Result(Result[3]),
    .C_prime_In(ula_cell_2_c_prime_out));  // open: C_prime_Out
  ula_cell ula_cell_2 (
    .C_prime_Out(ula_cell_2_c_prime_out), .B(shift_right_arith_1bit_1_out[2]), .A(A[2]), .OpCode(ULAOpCode),
    .Result(Result[2]), .C_prime_In(ula_cell_3_c_prime_out));
  ula_cell ula_cell_3 (
    .C_prime_Out(ula_cell_3_c_prime_out), .B(shift_right_arith_1bit_1_out[1]), .A(A[1]), .OpCode(ULAOpCode),
    .Result(Result[1]), .C_prime_In(ula_cell_4_c_prime_out));
  ula_cell ula_cell_4 (
    .C_prime_Out(ula_cell_4_c_prime_out), .B(shift_right_arith_1bit_1_out[0]), .A(A[0]), .OpCode(ULAOpCode),
    .Result(Result[0]), .C_prime_In(1'b0));

  // Notes on the sheet:
  //   00 = AND
  //   01 = OR
  //   10 = SOMA
  //   11 = XOR
  //   100 = SLL
endmodule

module ula_cell (
  input  B,
  input  A,
  input  C_prime_In,
  input  [2:0] OpCode,
  output C_prime_Out,
  output Result
);

  wire adder_1_sum, and_1_out, or_1_out, xor_1_out;

  and and_1 (and_1_out, A, B);
  or or_1 (or_1_out, A, B);
  adder adder_1 (.A(A), .B(B), .Carry_In(C_prime_In), .Carry_Out(C_prime_Out), .Sum(adder_1_sum));
  xor xor_1 (xor_1_out, A, B);
  Multiplexer #(.select(3), .enable("false")) multiplexer_1 (
    .in0(and_1_out), .in1(or_1_out), .in2(adder_1_sum), .in3(xor_1_out), .in4(B), .in5(B), .in6(B), .in7(B),
    .out(Result), .sel(OpCode));
endmodule

module mux_4_1 (
  input  _0,
  input  _1,
  input  _2,
  input  _3,
  input  [1:0] in_5,
  output Output
);

  wire and_1_out, and_2_out, and_3_out, and_4_out;

  and and_1 (and_1_out, _0, ~in_5[1], ~in_5[0]);  // AND_Gate
  and and_2 (and_2_out, _1, ~in_5[1], in_5[0]);  // AND_Gate
  and and_3 (and_3_out, _2, in_5[1], ~in_5[0]);  // AND_Gate
  and and_4 (and_4_out, _3, in_5[1], in_5[0]);
  or or_1 (Output, and_1_out, and_2_out, and_3_out, and_4_out);
endmodule

module adder (
  input  Carry_In,
  input  A,
  input  B,
  output Sum,
  output Carry_Out
);

  wire AB_out, AC_out, BC_out, xor_1_out;

  xor xor_1 (xor_1_out, A, B);
  and AB (AB_out, A, B);
  and BC (BC_out, B, Carry_In);
  and AC (AC_out, A, Carry_In);
  xor xor_2 (Sum, xor_1_out, Carry_In);
  or or_1 (Carry_Out, AB_out, BC_out, AC_out);
endmodule

module shift_rigtht_logical_1bit (
  input  [3:0] In,
  input  Shift,
  output [3:0] Out
);

  Multiplexer #(.width(4), .enable("false")) multiplexer_1 (.in0(In), .in1({1'b0, In[3:1]}), .out(Out), .sel(Shift));
endmodule

module shift_letf_logical_1bit (
  input  [3:0] In,
  input  Shift,
  output [3:0] Out
);

  Multiplexer #(.width(4), .enable("false")) multiplexer_1 (.in0(In), .in1({In[2:0], 1'b0}), .out(Out), .sel(Shift));
endmodule

module shift_right_arith_1bit (
  input  [3:0] In,
  input  Shift,
  output [3:0] Out
);

  Multiplexer #(.width(4), .enable("false")) multiplexer_1 (
    .in0(In), .in1({{2{In[3]}}, In[2:1]}), .out(Out), .sel(Shift));
endmodule

module SLLDetect (
  input  [2:0] ULAOpCode,
  output SLL
);

  and and_1 (SLL, ~ULAOpCode[0], ~ULAOpCode[1], ULAOpCode[2]);  // AND_Gate
endmodule
