// Logisim project via-dados-32bits.circ as structural Verilog: 24 circuits, main circuit ula
module via_dados (
  input  CLK,
  input  Reset,
  output out_3,
  output [31:0] out_4,
  output out_5,
  output out_6,
  output [31:0] out_7
);

  wire not_1_out;
  wire [7:0] adder_1_out, register_1_q;
  wire [31:0] banco_32bit_1_viewreg1, banco_32bit_1_viewreg2, extensor_1_out, multiplexer_1_out;

  Register register_1 (.D(adder_1_out), .Q(register_1_q), .clk(not_1_out), .clr(Reset));  // open: en
  Adder adder_1 (.a(register_1_q), .b(8'h1), .out(adder_1_out), .cin(1'b0));  // open: cout
  not not_1 (not_1_out, CLK);
  banco_32bit banco_32bit_1 (
    .CLK(CLK), .ViewReg1(banco_32bit_1_viewreg1), .Zero1(out_5), .ViewReg2(banco_32bit_1_viewreg2),
    .Zero2(out_6), .Data(out_4), .Reset(Reset), .WReg(out_7[26:22]), .Reg1(out_7[21:17]), .Reg2(out_7[16:12]));
  extensor extensor_1 (.Out(extensor_1_out), .In(out_7[11:1]));
  RAM #(.dataWidth(32)) ram_1 (.addr(register_1_q), .data(out_7));  // open: sel, clk, ld, clr
  ula ula_1 (.A(banco_32bit_1_viewreg1), .B(multiplexer_1_out), .Out(out_4), .ULA_OpCode(out_7[31:27]), .Zero(out_3));
  Multiplexer #(.width(32), .enable("false")) multiplexer_1 (
    .in0(banco_32bit_1_viewreg2), .in1(extensor_1_out), .out(multiplexer_1_out), .sel(out_7[0]));
endmodule

module banco_32bit (
  input  [31:0] Data,
  input  Reset,
  input  [4:0] Reg1,
  input  [4:0] Reg2,
  input  CLK,
  input  [4:0] WReg,
  output [31:0] ViewReg1,
  output Zero1,
  output [31:0] ViewReg2,
  output Zero2
);

  wire demultiplexer_1_out0, demultiplexer_1_out1, demultiplexer_1_out2, demultiplexer_1_out3,
       demultiplexer_1_out4, demultiplexer_1_out5, demultiplexer_1_out6, demultiplexer_1_out7,
       demultiplexer_1_out8, demultiplexer_1_out9, demultiplexer_1_out10, demultiplexer_1_out11,
       demultiplexer_1_out12, demultiplexer_1_out13, demultiplexer_1_out14, demultiplexer_1_out15,
       demultiplexer_1_out16, demultiplexer_1_out17, demultiplexer_1_out18, demultiplexer_1_out19,
       demultiplexer_1_out20, demultiplexer_1_out21, demultiplexer_1_out22, demultiplexer_1_out23,
       demultiplexer_1_out24, demultiplexer_1_out25, demultiplexer_1_out26, demultiplexer_1_out27,
       demultiplexer_1_out28, demultiplexer_1_out29, demultiplexer_1_out30, demultiplexer_1_out31;
  wire [31:0] registrador_32bit_1_out_4, registrador_32bit_2_out_4, registrador_32bit_3_out_4,
       registrador_32bit_4_out_4, registrador_32bit_5_out_4, registrador_32bit_6_out_4,
       registrador_32bit_7_out_4, registrador_32bit_8_out_4, registrador_32bit_9_out_4,
       registrador_32bit_10_out_4, registrador_32bit_11_out_4, registrador_32bit_12_out_4,
       registrador_32bit_13_out_4, registrador_32bit_14_out_4, registrador_32bit_15_out_4,
       registrador_32bit_16_out_4, registrador_32bit_17_out_4, registrador_32bit_18_out_4,
       registrador_32bit_19_out_4, registrador_32bit_20_out_4, registrador_32bit_21_out_4,
       registrador_32bit_22_out_4, registrador_32bit_23_out_4, registrador_32bit_24_out_4,
       registrador_32bit_25_out_4, registrador_32bit_26_out_4, registrador_32bit_27_out_4,
       registrador_32bit_28_out_4, registrador_32bit_29_out_4, registrador_32bit_30_out_4,
       registrador_32bit_31_out_4, registrador_32bit_32_out_4;

  Demultiplexer #(.select(5), .enable("false")) demultiplexer_1 (
    .out0(demultiplexer_1_out0), .out1(demultiplexer_1_out1), .out2(demultiplexer_1_out2),
    .out3(demultiplexer_1_out3), .out4(demultiplexer_1_out4), .out5(demultiplexer_1_out5),
    .out6(demultiplexer_1_out6), .out7(demultiplexer_1_out7), .out8(demultiplexer_1_out8),
    .out9(demultiplexer_1_out9), .out10(demultiplexer_1_out10), .out11(demultiplexer_1_out11),
    .out12(demultiplexer_1_out12), .out13(demultiplexer_1_out13), .out14(demultiplexer_1_out14),
    .out15(demultiplexer_1_out15), .out16(demultiplexer_1_out16), .out17(demultiplexer_1_out17),
    .out18(demultiplexer_1_out18), .out19(demultiplexer_1_out19), .out20(demultiplexer_1_out20),
    .out21(demultiplexer_1_out21), .out22(demultiplexer_1_out22), .out23(demultiplexer_1_out23),
    .out24(demultiplexer_1_out24), .out25(demultiplexer_1_out25), .out26(demultiplexer_1_out26),
    .out27(demultiplexer_1_out27), .out28(demultiplexer_1_out28), .out29(demultiplexer_1_out29),
    .out30(demultiplexer_1_out30), .out31(demultiplexer_1_out31), .in(CLK), .sel(WReg));
  registrador_32bit registrador_32bit_1 (
    .DataIn(Data), .Save(demultiplexer_1_out0), .Reset(Reset), .out_4(registrador_32bit_1_out_4));
  registrador_32bit registrador_32bit_2 (
    .DataIn(Data), .Save(demultiplexer_1_out1), .Reset(Reset), .out_4(registrador_32bit_2_out_4));
  registrador_32bit registrador_32bit_3 (
    .DataIn(Data), .Save(demultiplexer_1_out2), .Reset(Reset), .out_4(registrador_32bit_3_out_4));
  registrador_32bit registrador_32bit_4 (
    .DataIn(Data), .Save(demultiplexer_1_out3), .Reset(Reset), .out_4(registrador_32bit_4_out_4));
  registrador_32bit registrador_32bit_5 (
    .DataIn(Data), .Save(demultiplexer_1_out4), .Reset(Reset), .out_4(registrador_32bit_5_out_4));
  registrador_32bit registrador_32bit_6 (
    .DataIn(Data), .Save(demultiplexer_1_out5), .Reset(Reset), .out_4(registrador_32bit_6_out_4));
  registrador_32bit registrador_32bit_7 (
    .DataIn(Data), .Save(demultiplexer_1_out6), .Reset(Reset), .out_4(registrador_32bit_7_out_4));
  registrador_32bit registrador_32bit_8 (
    .DataIn(Data), .Save(demultiplexer_1_out7), .Reset(Reset), .out_4(registrador_32bit_8_out_4));
  registrador_32bit registrador_32bit_9 (
    .DataIn(Data), .Save(demultiplexer_1_out8), .Reset(Reset), .out_4(registrador_32bit_9_out_4));
  registrador_32bit registrador_32bit_10 (
    .DataIn(Data), .Save(demultiplexer_1_out9), .Reset(Reset), .out_4(registrador_32bit_10_out_4));
  registrador_32bit registrador_32bit_11 (
    .DataIn(Data), .Save(demultiplexer_1_out10), .Reset(Reset), .out_4(registrador_32bit_11_out_4));
  registrador_32bit registrador_32bit_12 (
    .DataIn(Data), .Save(demultiplexer_1_out11), .Reset(Reset), .out_4(registrador_32bit_12_out_4));
  registrador_32bit registrador_32bit_13 (
    .DataIn(Data), .Save(demultiplexer_1_out12), .Reset(Reset), .out_4(registrador_32bit_13_out_4));
  registrador_32bit registrador_32bit_14 (
    .DataIn(Data), .Save(demultiplexer_1_out13), .Reset(Reset), .out_4(registrador_32bit_14_out_4));
  registrador_32bit registrador_32bit_15 (
    .DataIn(Data), .Save(demultiplexer_1_out14), .Reset(Reset), .out_4(registrador_32bit_15_out_4));
  registrador_32bit registrador_32bit_16 (
    .DataIn(Data), .Save(demultiplexer_1_out15), .Reset(Reset), .out_4(registrador_32bit_16_out_4));
  registrador_32bit registrador_32bit_17 (
    .DataIn(Data), .Save(demultiplexer_1_out16), .Reset(Reset), .out_4(registrador_32bit_17_out_4));
  registrador_32bit registrador_32bit_18 (
    .DataIn(Data), .Save(demultiplexer_1_out17), .Reset(Reset), .out_4(registrador_32bit_18_out_4));
  registrador_32bit registrador_32bit_19 (
    .DataIn(Data), .Save(demultiplexer_1_out18), .Reset(Reset), .out_4(registrador_32bit_19_out_4));
  registrador_32bit registrador_32bit_20 (
    .DataIn(Data), .Save(demultiplexer_1_out19), .Reset(Reset), .out_4(registrador_32bit_20_out_4));
  registrador_32bit registrador_32bit_21 (
    .DataIn(Data), .Save(demultiplexer_1_out20), .Reset(Reset), .out_4(registrador_32bit_21_out_4));
  registrador_32bit registrador_32bit_22 (
    .DataIn(Data), .Save(demultiplexer_1_out21), .Reset(Reset), .out_4(registrador_32bit_22_out_4));
  registrador_32bit registrador_32bit_23 (
    .DataIn(Data), .Save(demultiplexer_1_out22), .Reset(Reset), .out_4(registrador_32bit_23_out_4));
  registrador_32bit registrador_32bit_24 (
    .DataIn(Data), .Save(demultiplexer_1_out23), .Reset(Reset), .out_4(registrador_32bit_24_out_4));
  registrador_32bit registrador_32bit_25 (
    .DataIn(Data), .Save(demultiplexer_1_out24), .Reset(Reset), .out_4(registrador_32bit_25_out_4));
  registrador_32bit registrador_32bit_26 (
    .DataIn(Data), .Save(demultiplexer_1_out25), .Reset(Reset), .out_4(registrador_32bit_26_out_4));
  registrador_32bit registrador_32bit_27 (
    .DataIn(Data), .Save(demultiplexer_1_out26), .Reset(Reset), .out_4(registrador_32bit_27_out_4));
  registrador_32bit registrador_32bit_28 (
    .DataIn(Data), .Save(demultiplexer_1_out27), .Reset(Reset), .out_4(registrador_32bit_28_out_4));
  registrador_32bit registrador_32bit_29 (
    .DataIn(Data), .Save(demultiplexer_1_out28), .Reset(Reset), .out_4(registrador_32bit_29_out_4));
  registrador_32bit registrador_32bit_30 (
    .DataIn(Data), .Save(demultiplexer_1_out29), .Reset(Reset), .out_4(registrador_32bit_30_out_4));
  registrador_32bit registrador_32bit_31 (
    .DataIn(Data), .Save(demultiplexer_1_out30), .Reset(Reset), .out_4(registrador_32bit_31_out_4));
  registrador_32bit registrador_32bit_32 (
    .DataIn(Data), .Save(demultiplexer_1_out31), .Reset(Reset), .out_4(registrador_32bit_32_out_4));
  Multiplexer #(.select(5), .width(32), .enable("false")) multiplexer_1 (
    .in0(registrador_32bit_1_out_4), .in1(registrador_32bit_2_out_4), .in2(registrador_32bit_3_out_4),
    .in3(registrador_32bit_4_out_4), .in4(registrador_32bit_5_out_4), .in5(registrador_32bit_6_out_4),
    .in6(registrador_32bit_7_out_4), .in7(registrador_32bit_8_out_4), .in8(registrador_32bit_9_out_4),
    .in9(registrador_32bit_10_out_4), .in10(registrador_32bit_11_out_4), .in11(registrador_32bit_12_out_4),
    .in12(registrador_32bit_13_out_4), .in13(registrador_32bit_14_out_4), .in14(registrador_32bit_15_out_4),
    .in15(registrador_32bit_16_out_4), .in16(registrador_32bit_17_out_4), .in17(registrador_32bit_18_out_4),
    .in18(registrador_32bit_19_out_4), .in19(registrador_32bit_20_out_4), .in20(registrador_32bit_21_out_4),
    .in21(registrador_32bit_22_out_4), .in22(registrador_32bit_23_out_4), .in23(registrador_32bit_24_out_4),
    .in24(registrador_32bit_25_out_4), .in25(registrador_32bit_26_out_4), .in26(registrador_32bit_27_out_4),
    .in27(registrador_32bit_28_out_4), .in28(registrador_32bit_29_out_4), .in29(registrador_32bit_30_out_4),
    .in30(registrador_32bit_31_out_4), .in31(registrador_32bit_32_out_4), .out(ViewReg1), .sel(Reg1));
  Multiplexer #(.select(5), .width(32), .enable("false")) multiplexer_2 (
    .in0(registrador_32bit_1_out_4), .in1(registrador_32bit_2_out_4), .in2(registrador_32bit_3_out_4),
    .in3(registrador_32bit_4_out_4), .in4(registrador_32bit_5_out_4), .in5(registrador_32bit_6_out_4),
    .in6(registrador_32bit_7_out_4), .in7(registrador_32bit_8_out_4), .in8(registrador_32bit_9_out_4),
    .in9(registrador_32bit_10_out_4), .in10(registrador_32bit_11_out_4), .in11(registrador_32bit_12_out_4),
    .in12(registrador_32bit_13_out_4), .in13(registrador_32bit_14_out_4), .in14(registrador_32bit_15_out_4),
    .in15(registrador_32bit_16_out_4), .in16(registrador_32bit_17_out_4), .in17(registrador_32bit_18_out_4),
    .in18(registrador_32bit_19_out_4), .in19(registrador_32bit_20_out_4), .in20(registrador_32bit_21_out_4),
    .in21(registrador_32bit_22_out_4), .in22(registrador_32bit_23_out_4), .in23(registrador_32bit_24_out_4),
    .in24(registrador_32bit_25_out_4), .in25(registrador_32bit_26_out_4), .in26(registrador_32bit_27_out_4),
    .in27(registrador_32bit_28_out_4), .in28(registrador_32bit_29_out_4), .in29(registrador_32bit_30_out_4),
    .in30(registrador_32bit_31_out_4), .in31(registrador_32bit_32_out_4), .out(ViewReg2), .sel(Reg2));
  and and_1 (Zero1, ~ViewReg1[16], ~ViewReg1[31], ~ViewReg1[30], ~ViewReg1[29], ~ViewReg1[28], ~ViewReg1[27], ~ViewReg1[26], ~ViewReg1[25], ~ViewReg1[24], ~ViewReg1[23], ~ViewReg1[22], ~ViewReg1[21], ~ViewReg1[20], ~ViewReg1[19], ~ViewReg1[18], ~ViewReg1[17], ~ViewReg1[15], ~ViewReg1[14], ~ViewReg1[13], ~ViewReg1[12], ~ViewReg1[11], ~ViewReg1[10], ~ViewReg1[9], ~ViewReg1[8], ~ViewReg1[7], ~ViewReg1[6], ~ViewReg1[5], ~ViewReg1[4], ~ViewReg1[3], ~ViewReg1[2], ~ViewReg1[1], ~ViewReg1[0]);  // AND_Gate
  and and_2 (Zero2, ~ViewReg2[16], ~ViewReg2[31], ~ViewReg2[30], ~ViewReg2[29], ~ViewReg2[28], ~ViewReg2[27], ~ViewReg2[26], ~ViewReg2[25], ~ViewReg2[24], ~ViewReg2[23], ~ViewReg2[22], ~ViewReg2[21], ~ViewReg2[20], ~ViewReg2[19], ~ViewReg2[18], ~ViewReg2[17], ~ViewReg2[15], ~ViewReg2[14], ~ViewReg2[13], ~ViewReg2[12], ~ViewReg2[11], ~ViewReg2[10], ~ViewReg2[9], ~ViewReg2[8], ~ViewReg2[7], ~ViewReg2[6], ~ViewReg2[5], ~ViewReg2[4], ~ViewReg2[3], ~ViewReg2[2], ~ViewReg2[1], ~ViewReg2[0]);  // AND_Gate
endmodule

module registrador_32bit (
  input  [31:0] DataIn,
  input  Save,
  input  Reset,
  output [31:0] out_4
);

  D_Flip_Flop d_ff_1 (.clk(Save), .D(DataIn[31]), .Q(out_4[31]), .reset(Reset));  // open: Qn, preset, en
  D_Flip_Flop d_ff_2 (.clk(Save), .D(DataIn[30]), .Q(out_4[30]), .reset(Reset));  // open: Qn, preset, en
  D_Flip_Flop d_ff_3 (.clk(Save), .D(DataIn[29]), .Q(out_4[29]), .reset(Reset));  // open: Qn, preset, en
  D_Flip_Flop d_ff_4 (.clk(Save), .D(DataIn[28]), .Q(out_4[28]), .reset(Reset));  // open: Qn, preset, en
  D_Flip_Flop d_ff_5 (.clk(Save), .D(DataIn[27]), .Q(out_4[27]), .reset(Reset));  // open: Qn, preset, en
  D_Flip_Flop d_ff_6 (.clk(Save), .D(DataIn[26]), .Q(out_4[26]), .reset(Reset));  // open: Qn, preset, en
  D_Flip_Flop d_ff_7 (.clk(Save), .D(DataIn[25]), .Q(out_4[25]), .reset(Reset));  // open: Qn, preset, en
  D_Flip_Flop d_ff_8 (.clk(Save), .D(DataIn[24]), .Q(out_4[24]), .reset(Reset));  // open: Qn, preset, en
  D_Flip_Flop d_ff_9 (.clk(Save), .D(DataIn[23]), .Q(out_4[23]), .reset(Reset));  // open: Qn, preset, en
  D_Flip_Flop d_ff_10 (.clk(Save), .D(DataIn[22]), .Q(out_4[22]), .reset(Reset));  // open: Qn, preset, en
  D_Flip_Flop d_ff_11 (.clk(Save), .D(DataIn[21]), .Q(out_4[21]), .reset(Reset));  // open: Qn, preset, en
  D_Flip_Flop d_ff_12 (.clk(Save), .D(DataIn[20]), .Q(out_4[20]), .reset(Reset));  // open: Qn, preset, en
  D_Flip_Flop d_ff_13 (.clk(Save), .D(DataIn[19]), .Q(out_4[19]), .reset(Reset));  // open: Qn, preset, en
  D_Flip_Flop d_ff_14 (.clk(Save), .D(DataIn[18]), .Q(out_4[18]), .reset(Reset));  // open: Qn, preset, en
  D_Flip_Flop d_ff_15 (.clk(Save), .D(DataIn[17]), .Q(out_4[17]), .reset(Reset));  // open: Qn, preset, en
  D_Flip_Flop d_ff_16 (.clk(Save), .D(DataIn[16]), .Q(out_4[16]), .reset(Reset));  // open: Qn, preset, en
  D_Flip_Flop d_ff_17 (.clk(Save), .D(DataIn[15]), .Q(out_4[15]), .reset(Reset));  // open: Qn, preset, en
  D_Flip_Flop d_ff_18 (.clk(Save), .D(DataIn[14]), .Q(out_4[14]), .reset(Reset));  // open: Qn, preset, en
  D_Flip_Flop d_ff_19 (.clk(Save), .D(DataIn[13]), .Q(out_4[13]), .reset(Reset));  // open: Qn, preset, en
  D_Flip_Flop d_ff_20 (.clk(Save), .D(DataIn[12]), .Q(out_4[12]), .reset(Reset));  // open: Qn, preset, en
  D_Flip_Flop d_ff_21 (.clk(Save), .D(DataIn[11]), .Q(out_4[11]), .reset(Reset));  // open: Qn, preset, en
  D_Flip_Flop d_ff_22 (.clk(Save), .D(DataIn[10]), .Q(out_4[10]), .reset(Reset));  // open: Qn, preset, en
  D_Flip_Flop d_ff_23 (.clk(Save), .D(DataIn[9]), .Q(out_4[9]), .reset(Reset));  // open: Qn, preset, en
  D_Flip_Flop d_ff_24 (.clk(Save), .D(DataIn[8]), .Q(out_4[8]), .reset(Reset));  // open: Qn, preset, en
  D_Flip_Flop d_ff_25 (.clk(Save), .D(DataIn[7]), .Q(out_4[7]), .reset(Reset));  // open: Qn, preset, en
  D_Flip_Flop d_ff_26 (.clk(Save), .D(DataIn[6]), .Q(out_4[6]), .reset(Reset));  // open: Qn, preset, en
  D_Flip_Flop d_ff_27 (.clk(Save), .D(DataIn[5]), .Q(out_4[5]), .reset(Reset));  // open: Qn, preset, en
  D_Flip_Flop d_ff_28 (.clk(Save), .D(DataIn[4]), .Q(out_4[4]), .reset(Reset));  // open: Qn, preset, en
  D_Flip_Flop d_ff_29 (.clk(Save), .D(DataIn[3]), .Q(out_4[3]), .reset(Reset));  // open: Qn, preset, en
  D_Flip_Flop d_ff_30 (.clk(Save), .D(DataIn[2]), .Q(out_4[2]), .reset(Reset));  // open: Qn, preset, en
  D_Flip_Flop d_ff_31 (.clk(Save), .D(DataIn[1]), .Q(out_4[1]), .reset(Reset));  // open: Qn, preset, en
  D_Flip_Flop d_ff_32 (.clk(Save), .D(DataIn[0]), .Q(out_4[0]), .reset(Reset));  // open: Qn, preset, en
endmodule

module ula (
  input  [31:0] A,
  input  [31:0] B,
  input  [4:0] ULA_OpCode,
  output Zero,
  output [31:0] Out
);

  wire sla_a_d_1_shift, sla_b_d_1_shift, sll_a_d_1_shift, sll_b_d_1_shift, sra_a_d_1_shift, sra_b_d_1_shift,
       srl_a_d_1_shift, srl_b_d_1_shift, ula_cell_2_c_prime_out, ula_cell_3_c_prime_out,
       ula_cell_4_c_prime_out, ula_cell_5_c_prime_out, ula_cell_6_c_prime_out, ula_cell_7_c_prime_out,
       ula_cell_8_c_prime_out, ula_cell_9_c_prime_out, ula_cell_10_c_prime_out, ula_cell_11_c_prime_out,
       ula_cell_12_c_prime_out, ula_cell_13_c_prime_out, ula_cell_14_c_prime_out, ula_cell_15_c_prime_out,
       ula_cell_16_c_prime_out, ula_cell_17_c_prime_out, ula_cell_18_c_prime_out, ula_cell_19_c_prime_out,
       ula_cell_20_c_prime_out, ula_cell_21_c_prime_out, ula_cell_22_c_prime_out, ula_cell_23_c_prime_out,
       ula_cell_24_c_prime_out, ula_cell_25_c_prime_out, ula_cell_26_c_prime_out, ula_cell_27_c_prime_out,
       ula_cell_28_c_prime_out, ula_cell_29_c_prime_out, ula_cell_30_c_prime_out, ula_cell_31_c_prime_out,
       ula_cell_32_c_prime_out;
  wire [31:0] shift_left_arith_1_out, shift_left_arith_2_out, shift_left_logical_1_out,
       shift_left_logical_2_out, shift_right_arith_1_out, shift_right_arith_2_out, shift_right_logical_1_out,
       shift_right_logical_2_out;

  shift_left_logical shift_left_logical_1 (.In(A), .Out(shift_left_logical_1_out), .Shift(sll_a_d_1_shift));
  shift_right_logical shift_right_logical_1 (
    .In(shift_left_logical_1_out), .Out(shift_right_logical_1_out), .Shift(srl_a_d_1_shift));
  sll_a_d sll_a_d_1 (.Shift(sll_a_d_1_shift), .OpCode(ULA_OpCode));
  srl_a_d srl_a_d_1 (.Shift(srl_a_d_1_shift), .UlaOpCode(ULA_OpCode));
  shift_right_logical shift_right_logical_2 (
    .In(shift_left_logical_2_out), .Out(shift_right_logical_2_out), .Shift(srl_b_d_1_shift));
  shift_left_logical shift_left_logical_2 (.In(B), .Out(shift_left_logical_2_out), .Shift(sll_b_d_1_shift));
  srl_b_d srl_b_d_1 (.Shift(srl_b_d_1_shift), .UlaOpCode(ULA_OpCode));
  sll_b_d sll_b_d_1 (.Shift(sll_b_d_1_shift), .UlaOpCode(ULA_OpCode));
  shift_right_arith shift_right_arith_1 (
    .In(shift_left_arith_1_out), .Out(shift_right_arith_1_out), .Shift(sra_a_d_1_shift));
  shift_left_arith shift_left_arith_1 (
    .In(shift_right_logical_1_out), .Out(shift_left_arith_1_out), .Shift(sla_a_d_1_shift));
  sra_a_d sra_a_d_1 (.Shift(sra_a_d_1_shift), .UlaOpCode(ULA_OpCode));
  sla_a_d sla_a_d_1 (.Shift(sla_a_d_1_shift), .UlaOpCode(ULA_OpCode));
  shift_left_arith shift_left_arith_2 (
    .In(shift_right_logical_2_out), .Out(shift_left_arith_2_out), .Shift(sla_b_d_1_shift));
  shift_right_arith shift_right_arith_2 (
    .In(shift_left_arith_2_out), .Out(shift_right_arith_2_out), .Shift(sra_b_d_1_shift));
  sra_b_d sra_b_d_1 (.Shift(sra_b_d_1_shift), .UlaOpCode(ULA_OpCode));
  sla_b_d sla_b_d_1 (.Shift(sla_b_d_1_shift), .UlaOpCode(ULA_OpCode));
  ula_cell ula_cell_1 (
    .B(shift_right_arith_2_out[31]), .A(shift_right_arith_1_out[31]), .OpCode(ULA_OpCode), .Out(Out[31]),
    .C_prime_in(ula_cell_2_c_prime_out));  // open: C_prime_out
  ula_cell ula_cell_2 (
    .C_prime_out(ula_cell_2_c_prime_out), .B(shift_right_arith_2_out[30]), .A(shift_right_arith_1_out[30]),
    .OpCode(ULA_OpCode), .Out(Out[30]), .C_prime_in(ula_cell_3_c_prime_out));
  ula_cell ula_cell_3 (
    .C_prime_out(ula_cell_3_c_prime_out), .B(shift_right_arith_2_out[29]), .A(shift_right_arith_1_out[29]),
    .OpCode(ULA_OpCode), .Out(Out[29]), .C_prime_in(ula_cell_5_c_prime_out));
  ula_cell ula_cell_4 (
    .C_prime_out(ula_cell_4_c_prime_out), .B(shift_right_arith_2_out[27]), .A(shift_right_arith_1_out[27]),
    .OpCode(ULA_OpCode), .Out(Out[27]), .C_prime_in(ula_cell_6_c_prime_out));
  ula_cell ula_cell_5 (
    .C_prime_out(ula_cell_5_c_prime_out), .B(shift_right_arith_2_out[28]), .A(shift_right_arith_1_out[28]),
    .OpCode(ULA_OpCode), .Out(Out[28]), .C_prime_in(ula_cell_4_c_prime_out));
  ula_cell ula_cell_6 (
    .C_prime_out(ula_cell_6_c_prime_out), .B(shift_right_arith_2_out[26]), .A(shift_right_arith_1_out[26]),
    .OpCode(ULA_OpCode), .Out(Out[26]), .C_prime_in(ula_cell_7_c_prime_out));
  ula_cell ula_cell_7 (
    .C_prime_out(ula_cell_7_c_prime_out), .B(shift_right_arith_2_out[25]), .A(shift_right_arith_1_out[25]),
    .OpCode(ULA_OpCode), .Out(Out[25]), .C_prime_in(ula_cell_8_c_prime_out));
  ula_cell ula_cell_8 (
    .C_prime_out(ula_cell_8_c_prime_out), .B(shift_right_arith_2_out[24]), .A(shift_right_arith_1_out[24]),
    .OpCode(ULA_OpCode), .Out(Out[24]), .C_prime_in(ula_cell_10_c_prime_out));
  ula_cell ula_cell_9 (
    .C_prime_out(ula_cell_9_c_prime_out), .B(shift_right_arith_2_out[22]), .A(shift_right_arith_1_out[22]),
    .OpCode(ULA_OpCode), .Out(Out[22]), .C_prime_in(ula_cell_11_c_prime_out));
  ula_cell ula_cell_10 (
    .C_prime_out(ula_cell_10_c_prime_out), .B(shift_right_arith_2_out[23]), .A(shift_right_arith_1_out[23]),
    .OpCode(ULA_OpCode), .Out(Out[23]), .C_prime_in(ula_cell_9_c_prime_out));
  ula_cell ula_cell_11 (
    .C_prime_out(ula_cell_11_c_prime_out), .B(shift_right_arith_2_out[21]), .A(shift_right_arith_1_out[21]),
    .OpCode(ULA_OpCode), .Out(Out[21]), .C_prime_in(ula_cell_13_c_prime_out));
  ula_cell ula_cell_12 (
    .C_prime_out(ula_cell_12_c_prime_out), .B(shift_right_arith_2_out[19]), .A(shift_right_arith_1_out[19]),
    .OpCode(ULA_OpCode), .Out(Out[19]), .C_prime_in(ula_cell_14_c_prime_out));
  ula_cell ula_cell_13 (
    .C_prime_out(ula_cell_13_c_prime_out), .B(shift_right_arith_2_out[20]), .A(shift_right_arith_1_out[20]),
    .OpCode(ULA_OpCode), .Out(Out[20]), .C_prime_in(ula_cell_12_c_prime_out));
  ula_cell ula_cell_14 (
    .C_prime_out(ula_cell_14_c_prime_out), .B(shift_right_arith_2_out[18]), .A(shift_right_arith_1_out[18]),
    .OpCode(ULA_OpCode), .Out(Out[18]), .C_prime_in(ula_cell_15_c_prime_out));
  ula_cell ula_cell_15 (
    .C_prime_out(ula_cell_15_c_prime_out), .B(shift_right_arith_2_out[17]), .A(shift_right_arith_1_out[17]),
    .OpCode(ULA_OpCode), .Out(Out[17]), .C_prime_in(ula_cell_16_c_prime_out));
  ula_cell ula_cell_16 (
    .C_prime_out(ula_cell_16_c_prime_out), .B(shift_right_arith_2_out[16]), .A(shift_right_arith_1_out[16]),
    .OpCode(ULA_OpCode), .Out(Out[16]), .C_prime_in(ula_cell_18_c_prime_out));
  ula_cell ula_cell_17 (
    .C_prime_out(ula_cell_17_c_prime_out), .B(shift_right_arith_2_out[14]), .A(shift_right_arith_1_out[14]),
    .OpCode(ULA_OpCode), .Out(Out[14]), .C_prime_in(ula_cell_19_c_prime_out));
  ula_cell ula_cell_18 (
    .C_prime_out(ula_cell_18_c_prime_out), .B(shift_right_arith_2_out[15]), .A(shift_right_arith_1_out[15]),
    .OpCode(ULA_OpCode), .Out(Out[15]), .C_prime_in(ula_cell_17_c_prime_out));
  ula_cell ula_cell_19 (
    .C_prime_out(ula_cell_19_c_prime_out), .B(shift_right_arith_2_out[13]), .A(shift_right_arith_1_out[13]),
    .OpCode(ULA_OpCode), .Out(Out[13]), .C_prime_in(ula_cell_20_c_prime_out));
  ula_cell ula_cell_20 (
    .C_prime_out(ula_cell_20_c_prime_out), .B(shift_right_arith_2_out[12]), .A(shift_right_arith_1_out[12]),
    .OpCode(ULA_OpCode), .Out(Out[12]), .C_prime_in(ula_cell_21_c_prime_out));
  ula_cell ula_cell_21 (
    .C_prime_out(ula_cell_21_c_prime_out), .B(shift_right_arith_2_out[11]), .A(shift_right_arith_1_out[11]),
    .OpCode(ULA_OpCode), .Out(Out[11]), .C_prime_in(ula_cell_22_c_prime_out));
  ula_cell ula_cell_22 (
    .C_prime_out(ula_cell_22_c_prime_out), .B(shift_right_arith_2_out[10]), .A(shift_right_arith_1_out[10]),
    .OpCode(ULA_OpCode), .Out(Out[10]), .C_prime_in(ula_cell_24_c_prime_out));
  ula_cell ula_cell_23 (
    .C_prime_out(ula_cell_23_c_prime_out), .B(shift_right_arith_2_out[8]), .A(shift_right_arith_1_out[8]),
    .OpCode(ULA_OpCode), .Out(Out[8]), .C_prime_in(ula_cell_26_c_prime_out));
  ula_cell ula_cell_24 (
    .C_prime_out(ula_cell_24_c_prime_out), .B(shift_right_arith_2_out[9]), .A(shift_right_arith_1_out[9]),
    .OpCode(ULA_OpCode), .Out(Out[9]), .C_prime_in(ula_cell_23_c_prime_out));
  ula_cell ula_cell_25 (
    .C_prime_out(ula_cell_25_c_prime_out), .B(shift_right_arith_2_out[6]), .A(shift_right_arith_1_out[6]),
    .OpCode(ULA_OpCode), .Out(Out[6]), .C_prime_in(ula_cell_27_c_prime_out));
  ula_cell ula_cell_26 (
    .C_prime_out(ula_cell_26_c_prime_out), .B(shift_right_arith_2_out[7]), .A(shift_right_arith_1_out[7]),
    .OpCode(ULA_OpCode), .Out(Out[7]), .C_prime_in(ula_cell_25_c_prime_out));
  ula_cell ula_cell_27 (
    .C_prime_out(ula_cell_27_c_prime_out), .B(shift_right_arith_2_out[5]), .A(shift_right_arith_1_out[5]),
    .OpCode(ULA_OpCode), .Out(Out[5]), .C_prime_in(ula_cell_28_c_prime_out));
  ula_cell ula_cell_28 (
    .C_prime_out(ula_cell_28_c_prime_out), .B(shift_right_arith_2_out[4]), .A(shift_right_arith_1_out[4]),
    .OpCode(ULA_OpCode), .Out(Out[4]), .C_prime_in(ula_cell_29_c_prime_out));
  ula_cell ula_cell_29 (
    .C_prime_out(ula_cell_29_c_prime_out), .B(shift_right_arith_2_out[3]), .A(shift_right_arith_1_out[3]),
    .OpCode(ULA_OpCode), .Out(Out[3]), .C_prime_in(ula_cell_30_c_prime_out));
  ula_cell ula_cell_30 (
    .C_prime_out(ula_cell_30_c_prime_out), .B(shift_right_arith_2_out[2]), .A(shift_right_arith_1_out[2]),
    .OpCode(ULA_OpCode), .Out(Out[2]), .C_prime_in(ula_cell_32_c_prime_out));
  ula_cell ula_cell_31 (
    .C_prime_out(ula_cell_31_c_prime_out), .B(shift_right_arith_2_out[0]), .A(shift_right_arith_1_out[0]),
    .OpCode(ULA_OpCode), .Out(Out[0]), .C_prime_in(1'b0));
  ula_cell ula_cell_32 (
    .C_prime_out(ula_cell_32_c_prime_out), .B(shift_right_arith_2_out[1]), .A(shift_right_arith_1_out[1]),
    .OpCode(ULA_OpCode), .Out(Out[1]), .C_prime_in(ula_cell_31_c_prime_out));
  and and_1 (Zero, ~Out[31], ~Out[30], ~Out[29], ~Out[28], ~Out[27], ~Out[26], ~Out[25], ~Out[24], ~Out[23], ~Out[22], ~Out[21], ~Out[20], ~Out[19], ~Out[18], ~Out[17], ~Out[16], ~Out[15], ~Out[14], ~Out[13], ~Out[12], ~Out[11], ~Out[10], ~Out[9], ~Out[8], ~Out[7], ~Out[6], ~Out[5], ~Out[4], ~Out[3], ~Out[2], ~Out[1], ~Out[0]);  // AND_Gate
  // NOT_Gate not_1 is placed but not wired
endmodule

module teste (
  input  [31:0] A,
  input  [31:0] B,
  input  [4:0] ULA_OpCode,
  output Zero,
  output [31:0] Out
);

  // ula ula_1: pin names not known; wires that end beside it: A, B, Out, Zero, ULA_OpCode

  // Notes on the sheet:
  //   00000 - AND
  //   00001 - OR
  //   00010- ADD
  //   00011 - XOR
  //   00100 - SLL A
  //   00101 - SLL B
  //   00110 - SRL A
  //   00111 - SRL B
  //   01000 - SLA A 
  //   01001 - SLA B
  //   01010 - SRA A 
  //   01011 - SRA B
endmodule

module adder (
  input  C_prime_in,
  input  A,
  input  B,
  output Sum,
  output C_prime_out
);

  wire and_1_out, and_2_out, xor_1_out;

  xor xor_1 (xor_1_out, A, B);
  xor xor_2 (Sum, xor_1_out, C_prime_in);
  and and_1 (and_1_out, xor_1_out, C_prime_in);
  and and_2 (and_2_out, A, B);
  or or_1 (C_prime_out, and_1_out, and_2_out);
endmodule

module mux_4_1 (
  input  _0,
  input  _1,
  input  _2,
  input  _3,
  input  [1:0] in_5,
  output Out
);

  wire and_1_out, and_2_out, and_3_out, and_4_out;

  and and_1 (and_1_out, _0, ~in_5[1], ~in_5[0]);  // AND_Gate
  and and_2 (and_2_out, _1, ~in_5[1], in_5[0]);  // AND_Gate
  and and_3 (and_3_out, _2, in_5[1], ~in_5[0]);  // AND_Gate
  and and_4 (and_4_out, _3, in_5[1], in_5[0]);
  or or_1 (Out, and_1_out, and_2_out, and_3_out, and_4_out);
endmodule

module mux_8_1 (
  input  o,
  input  _1,
  input  _2,
  input  _3,
  input  _4,
  input  _5,
  input  _6,
  input  _7,
  input  [2:0] Select,
  output Out
);

  wire and_1_out, and_2_out, and_3_out, and_4_out, and_5_out, and_6_out, and_7_out, and_8_out;

  and and_1 (and_1_out, o, ~Select[2], ~Select[1], ~Select[0]);  // AND_Gate
  and and_2 (and_2_out, _1, ~Select[2], ~Select[1], Select[0]);  // AND_Gate
  and and_3 (and_3_out, _2, ~Select[2], Select[1], ~Select[0]);  // AND_Gate
  and and_4 (and_4_out, _3, ~Select[2], Select[1], Select[0]);  // AND_Gate
  and and_5 (and_5_out, _4, Select[2], ~Select[1], ~Select[0]);  // AND_Gate
  and and_6 (and_6_out, _5, Select[2], ~Select[1], Select[0]);  // AND_Gate
  and and_7 (and_7_out, _6, Select[2], Select[1], ~Select[0]);  // AND_Gate
  and and_8 (and_8_out, _7, Select[2], Select[1], Select[0]);
  or or_1 (Out, and_1_out, and_2_out, and_3_out, and_4_out, and_5_out, and_6_out, and_7_out, and_8_out);
endmodule

module mux_32_1 (
  input  o,
  input  _1,
  input  _2,
  input  _3,
  input  _4,
  input  _5,
  input  _6,
  input  _7,
  input  _8,
  input  _9,
  input  _10,
  input  _11,
  input  _12,
  input  _13,
  input  _14,
  input  _15,
  input  _16,
  input  _17,
  input  _18,
  input  _19,
  input  _20,
  input  _21,
  input  _22,
  input  _23,
  input  _24,
  input  _25,
  input  _26,
  input  _27,
  input  _28,
  input  _29,
  input  _30,
  input  _31,
  input  [4:0] Select,
  output Out
);

  wire mux_8_1_1_out, mux_8_1_2_out, mux_8_1_3_out, mux_8_1_4_out;

  mux_8_1 mux_8_1_1 (
    .o(o), ._1(_1), ._2(_2), ._3(_3), ._4(_4), ._5(_5), ._6(_6), ._7(_7), .Out(mux_8_1_1_out),
    .Select(Select[2:0]));
  mux_8_1 mux_8_1_2 (
    .o(_8), ._1(_9), ._2(_10), ._3(_11), ._4(_12), ._5(_13), ._6(_14), ._7(_15), .Out(mux_8_1_2_out),
    .Select(Select[2:0]));
  mux_4_1 mux_4_1_1 (
    ._0(mux_8_1_1_out), ._1(mux_8_1_2_out), ._2(mux_8_1_3_out), ._3(mux_8_1_4_out), .Out(Out),
    .in_5(Select[4:3]));
  mux_8_1 mux_8_1_3 (
    .o(_16), ._1(_17), ._2(_18), ._3(_19), ._4(_20), ._5(_21), ._6(_22), ._7(_23), .Out(mux_8_1_3_out),
    .Select(Select[2:0]));
  mux_8_1 mux_8_1_4 (
    .o(_24), ._1(_25), ._2(_26), ._3(_27), ._4(_28), ._5(_29), ._6(_30), ._7(_31), .Out(mux_8_1_4_out),
    .Select(Select[2:0]));
endmodule

module mux_2_32 (
  input  [31:0] A,
  input  [31:0] B,
  input  SEL,
  output [31:0] out_4
);

  wire [31:0] and_1_out, and_2_out;

  assign and_1_out = A & ~{32{SEL}};  // AND_Gate and_1, 32 bits wide
  assign and_2_out = B & {32{SEL}};  // AND_Gate and_2, 32 bits wide
  assign out_4 = and_1_out | and_2_out;  // OR_Gate or_1, 32 bits wide
endmodule

module ula_cell (
  input  B,
  input  A,
  input  C_prime_in,
  input  [4:0] OpCode,
  output C_prime_out,
  output Out
);

  wire adder_1_sum, and_1_out, nand_1_out, or_1_out, xor_1_out;

  and and_1 (and_1_out, A, B);
  or or_1 (or_1_out, A, B);
  adder adder_1 (.A(A), .B(B), .Sum(adder_1_sum), .C_prime_in(C_prime_in), .C_prime_out(C_prime_out));
  xor xor_1 (xor_1_out, A, B);
  nand nand_1 (nand_1_out, ~A, B);  // NAND_Gate
  mux_32_1 mux_32_1_1 (
    .o(and_1_out), ._1(or_1_out), ._2(adder_1_sum), ._3(xor_1_out), ._4(A), ._5(B), ._6(A), ._7(B), ._8(A),
    ._9(B), ._10(A), ._11(B), ._31(nand_1_out), .Out(Out), .Select(OpCode));  // open: _12, _13, _14, _15, _16, _17, _18, _19, _20, _21, _22, _23, _24, _25, _26, _27, _28, _29, _30

  // Notes on the sheet:
  //   00000 - AND
  //   00001 - OR
  //   00010- ADD
  //   00011 - XOR
  //   00100 - SLL A
  //   00101 - SLL B
  //   00110 - SRL A
  //   00111 - SRL B
  //   01000 - SLA A 
  //   01001 - SLA B
  //   01010 - SRA A 
  //   01011 - SRA B
  //   11111 - ~AB
endmodule

module shift_left_logical (
  input  [31:0] In,
  input  Shift,
  output [31:0] Out
);

  mux_2_32 mux_2_32_1 (.A(In), .B({In[30:0], 1'b0}), .out_4(Out), .SEL(Shift));
endmodule

module shift_left_arith (
  input  [31:0] In,
  input  Shift,
  output [31:0] Out
);

  mux_2_32 mux_2_32_1 (.A(In), .B({In[30:0], In[0]}), .out_4(Out), .SEL(Shift));
endmodule

module shift_right_logical (
  input  [31:0] In,
  input  Shift,
  output [31:0] Out
);

  mux_2_32 mux_2_32_1 (.A(In), .B({1'b0, In[31:1]}), .out_4(Out), .SEL(Shift));
endmodule

module shift_right_arith (
  input  [31:0] In,
  input  Shift,
  output [31:0] Out
);

  mux_2_32 mux_2_32_1 (.A(In), .B({{2{In[31]}}, In[30:1]}), .out_4(Out), .SEL(Shift));
endmodule

module sll_a_d (
  input  [4:0] OpCode,
  output Shift
);

  and and_1 (Shift, ~OpCode[4], ~OpCode[3], OpCode[2], ~OpCode[1], ~OpCode[0]);  // AND_Gate
endmodule

module sll_b_d (
  input  [4:0] UlaOpCode,
  output Shift
);

  and and_1 (Shift, ~UlaOpCode[4], ~UlaOpCode[3], UlaOpCode[2], ~UlaOpCode[1], UlaOpCode[0]);  // AND_Gate
endmodule

module srl_a_d (
  input  [4:0] UlaOpCode,
  output Shift
);

  and and_1 (Shift, ~UlaOpCode[4], ~UlaOpCode[3], UlaOpCode[2], UlaOpCode[1], ~UlaOpCode[0]);  // AND_Gate
endmodule

module srl_b_d (
  input  [4:0] UlaOpCode,
  output Shift
);

  and and_1 (Shift, ~UlaOpCode[4], ~UlaOpCode[3], UlaOpCode[2], UlaOpCode[1], UlaOpCode[0]);  // AND_Gate
endmodule

module sla_a_d (
  input  [4:0] UlaOpCode,
  output Shift
);

  and and_1 (Shift, ~UlaOpCode[4], UlaOpCode[3], ~UlaOpCode[2], ~UlaOpCode[1], ~UlaOpCode[0]);  // AND_Gate
endmodule

module sla_b_d (
  input  [4:0] UlaOpCode,
  output Shift
);

  and and_1 (Shift, ~UlaOpCode[4], UlaOpCode[3], ~UlaOpCode[2], ~UlaOpCode[1], UlaOpCode[0]);  // AND_Gate
endmodule

module sra_a_d (
  input  [4:0] UlaOpCode,
  output Shift
);

  and and_1 (Shift, ~UlaOpCode[4], UlaOpCode[3], ~UlaOpCode[2], UlaOpCode[1], ~UlaOpCode[0]);  // AND_Gate
endmodule

module sra_b_d (
  input  [4:0] UlaOpCode,
  output Shift
);

  and and_1 (Shift, ~UlaOpCode[4], UlaOpCode[3], ~UlaOpCode[2], UlaOpCode[1], UlaOpCode[0]);  // AND_Gate
endmodule

module extensor (
  input  [10:0] In,
  output [31:0] Out
);


  assign Out = {{22{In[10]}}, In[9:0]};
endmodule
